// Logisim project zhan_design.circ as structural Verilog: 17 circuits, main circuit main
module PC (
  input  [31:0] D,
  input  enable,
  input  clk,
  input  rst,
  output [31:0] pc_out
);

  register_32bits register_32bits_1 (.D(D), .enable(enable), .clk(clk), .rst(rst), .reg_out(pc_out));
endmodule

module register_32bits (
  input  [31:0] D,
  input  enable,
  input  clk,
  input  rst,
  output [31:0] reg_out
);

  Register #(.width(32)) register_1 (.D(D), .en(enable), .clk(clk), .Q(reg_out), .clr(rst));
endmodule

module main (
  input  rst,
  output [31:0] reg0_val,
  output [31:0] reg8_val,
  output [31:0] reg1_val,
  output [31:0] reg9_val,
  output [31:0] reg2_val,
  output [31:0] reg10_val,
  output [31:0] reg3_val,
  output [31:0] reg11_val,
  output [31:0] out_10,
  output [31:0] reg4_val,
  output [31:0] reg12_val,
  output [31:0] pc_out,
  output [31:0] reg5_val,
  output [31:0] reg13_val,
  output [31:0] instruction,
  output [31:0] reg6_val,
  output [31:0] reg14_val,
  output [31:0] reg7_val,
  output [31:0] reg15_val
);

  wire clk_out, reg_write_enabler_1_reg_write, which_instruction_1_add, which_instruction_1_addi,
       which_instruction_1_illegal, which_instruction_1_jalr, which_instruction_1_lbu,
       which_instruction_1_lui, which_instruction_1_lw, which_instruction_1_sb, which_instruction_1_sw,
       which_type_1_i_type, which_type_1_r_type, which_type_1_s_type, which_type_1_u_type;
  wire [2:0] my_decoder_1_funct3;
  wire [4:0] my_decoder_1_rd, my_decoder_1_rs1, my_decoder_1_rs2;
  wire [6:0] my_decoder_1_funct7, my_decoder_1_opcode;
  wire [31:0] alu_1_y, b_mux_1_b, data_memory_1_read_data, immediate_generator_1_imm, next_pc_1_pc_next,
       pc_plus_4_1_pc_plus_4_out, register_file_1_rs1_val, register_file_1_rs2_val, writeback_mux_1_rd_data;

  Clock clk (.out(clk_out));
  PC pc_1 (.D(next_pc_1_pc_next), .enable(1'b1), .clk(clk_out), .rst(rst), .pc_out(out_10));
  instruction_memory instruction_memory_1 (.pc(out_10), .instruction(instruction));
  my_decoder my_decoder_1 (
    .instruction(instruction), .opcode(my_decoder_1_opcode), .rd(my_decoder_1_rd),
    .funct3(my_decoder_1_funct3), .rs1(my_decoder_1_rs1), .rs2(my_decoder_1_rs2), .funct7(my_decoder_1_funct7));
  which_type which_type_1 (
    .opcode(my_decoder_1_opcode), .r_type(which_type_1_r_type), .i_type(which_type_1_i_type),
    .s_type(which_type_1_s_type), .u_type(which_type_1_u_type));
  register_file register_file_1 (
    .rs1_addr(my_decoder_1_rs1), .rs2_addr(my_decoder_1_rs2), .rd_addr(my_decoder_1_rd),
    .reg_write(reg_write_enabler_1_reg_write), .rd_data(writeback_mux_1_rd_data), .clk(clk_out), .rst(rst),
    .rs1_val(register_file_1_rs1_val), .rs2_val(register_file_1_rs2_val), .reg0_val(reg0_val),
    .reg1_val(reg1_val), .reg2_val(reg2_val), .reg3_val(reg3_val), .reg4_val(reg4_val), .reg5_val(reg5_val),
    .reg6_val(reg6_val), .reg7_val(reg7_val), .reg8_val(reg8_val), .reg9_val(reg9_val),
    .reg10_val(reg10_val), .reg11_val(reg11_val), .reg12_val(reg12_val), .reg13_val(reg13_val),
    .reg14_val(reg14_val), .reg15_val(reg15_val));
  immediate_generator immediate_generator_1 (
    .illegal(which_instruction_1_illegal), .r_type(which_type_1_r_type), .i_type(which_type_1_i_type),
    .instruction(instruction), .s_type(which_type_1_s_type), .u_type(which_type_1_u_type),
    .imm(immediate_generator_1_imm));
  which_instruction which_instruction_1 (
    .opcode(my_decoder_1_opcode), .funct3(my_decoder_1_funct3), .funct7(my_decoder_1_funct7),
    .add(which_instruction_1_add), .addi(which_instruction_1_addi), .lui(which_instruction_1_lui),
    .lw(which_instruction_1_lw), .lbu(which_instruction_1_lbu), .sw(which_instruction_1_sw),
    .sb(which_instruction_1_sb), .jalr(which_instruction_1_jalr), .illegal(which_instruction_1_illegal));
  b_mux b_mux_1 (
    .rs2_val(register_file_1_rs2_val), .imm(immediate_generator_1_imm), .addi(which_instruction_1_addi),
    .lw(which_instruction_1_lw), .lbu(which_instruction_1_lbu), .sw(which_instruction_1_sw),
    .sb(which_instruction_1_sb), .jalr(which_instruction_1_jalr), .b(b_mux_1_b));
  alu alu_1 (.a(register_file_1_rs1_val), .b(b_mux_1_b), .y(alu_1_y));
  data_memory data_memory_1 (
    .addr(alu_1_y), .write_data(register_file_1_rs2_val), .sw(which_instruction_1_sw),
    .sb(which_instruction_1_sb), .lw(which_instruction_1_lw), .lbu(which_instruction_1_lbu), .clk(clk_out),
    .read_data(data_memory_1_read_data));
  writeback_mux writeback_mux_1 (
    .y(alu_1_y), .imm(immediate_generator_1_imm), .read_data(data_memory_1_read_data),
    .pc_plus_4(pc_plus_4_1_pc_plus_4_out), .lw(which_instruction_1_lw), .lbu(which_instruction_1_lbu),
    .lui(which_instruction_1_lui), .jalr(which_instruction_1_jalr), .rd_data(writeback_mux_1_rd_data));
  pc_plus_4 pc_plus_4_1 (.pc(out_10), .pc_plus_4_out(pc_plus_4_1_pc_plus_4_out));
  next_pc next_pc_1 (
    .pc_plus_4(pc_plus_4_1_pc_plus_4_out), .y(alu_1_y), .jalr(which_instruction_1_jalr),
    .pc_next(next_pc_1_pc_next));
  reg_write_enabler reg_write_enabler_1 (
    .add(which_instruction_1_add), .addi(which_instruction_1_addi), .lui(which_instruction_1_lui),
    .lw(which_instruction_1_lw), .lbu(which_instruction_1_lbu), .jalr(which_instruction_1_jalr),
    .illegal(which_instruction_1_illegal), .reg_write(reg_write_enabler_1_reg_write));

  assign pc_out = out_10;
endmodule

module instruction_memory (
  input  [31:0] pc,
  output [31:0] instruction
);

  ROM #(.addrWidth(24), .dataWidth(32)) rom_1 (.addr(pc[25:2]), .data(instruction));

  // Notes on the sheet:
  //   contents of rom_1 (hex, n*v repeats v):
  //   413 52137 10113 10b7 22408093 80e7 fea12823 fe812e23 1437 40840413 ff014183 3401b3 1c183 ff114203
  //   440233 24203 4181b3 ff214203 440233 24203 4181b3 ff314203 440233 24203 4181b3 1237 40020213 320233
  //   24203 ffc12403 420233 420233 410233 a000193 fe312823 9c00193 fe312623 fec22203 20067 8067 ff410113
  //   100513 112423 10b7 21808093 80e7 fec10113 912423 494b7 6b048493 812623 112823 496b7 69068693 48413
  //   48713 fe012823 174183 fe3109a3 ff012183 fe812e23 fe312823 3d437 60040413 ff214203 420233 420233
  //   440233 22203 fe412623 ff114203 420233 420233 440233 22203 fe412423 ff014203 420233 420233 440233
  //   22203 fe412223 fed14183 fea14203 4181b3 fe714203 4181b3 fe312223 fee14183 feb14203 4181b3 fe3102a3
  //   fef14183 fe310323 fe412183 8237 20213 440433 ff314203 420233 420233 440233 22203 ffc12403 4181b3
  //   74503 350533 6a603 270713 468693 fe312a23 fec12423 31237 50020213 feb14183 4181b3 1c183 fe3103a3
  //   fea14183 4181b3 1c183 fe310323 fe914183 4181b3 1c183 fe3102a3 fe814183 4181b3 1c183 fe310223
  //   ff412183 fe412203 450533 150513 fea12823 fe812e23 1437 40840413 ff014183 3401b3 1c183 ff114203
  //   440233 24203 4181b3 ff214203 440233 24203 4181b3 ff314203 440233 24203 4181b3 1237 40020213 320233
  //   24503 ffc12403 e12223 d12023 1800093 80e7 412703 497b7 6c078793 12683 fee12823 fef12623 fe812e23
  //   fe912c23 1437 30040413 ff014183 340233 100193 320023 fec14183 3401b3 18023 24183 ff114483 940233
  //   100493 920023 fed14483 9404b3 48023 24483 9181b3 ff214483 940233 100493 920023 fee14483 9404b3 48023
  //   24483 9181b3 ff314483 940233 100493 920023 fef14483 9404b3 48023 24483 9181b3 1237 40020213 320233
  //   24203 ff812483 ffc12403 420233 420233 410233 37800193 fe312823 e000193 fe312623 fec22203 20067 49737
  //   67070713 72683 fe012823 14c203 fe4108a3 ff012203 4c503 450533 470713 e12023 fe312a23 fed12423 31237
  //   50020213 feb14183 4181b3 1c183 fe3103a3 fea14183 4181b3 1c183 fe310323 fe914183 4181b3 1c183
  //   fe3102a3 fe814183 4181b3 1c183 fe310223 ff412183 fe412203 450533 150513 fea12823 fe812e23 1437
  //   40840413 ff014183 3401b3 1c183 ff114203 440233 24203 4181b3 ff214203 440233 24203 4181b3 ff314203
  //   440233 24203 4181b3 1237 40020213 320233 24503 ffc12403 1800093 80e7 248493 497b7 6c078793 12703
  //   fe912823 fef12623 fe812e23 fe912c23 1437 30040413 ff014183 340233 100193 320023 fec14183 3401b3
  //   18023 24183 ff114483 940233 100493 920023 fed14483 9404b3 48023 24483 9181b3 ff214483 940233 100493
  //   920023 fee14483 9404b3 48023 24483 9181b3 ff314483 940233 100493 920023 fef14483 9404b3 48023 24483
  //   9181b3 1237 40020213 320233 24203 ff812483 ffc12403 420233 420233 410233 55c00193 fe312823 38000193
  //   fe312623 fec22203 20067 244683 144603 344703 444783 494b7 64048493 8*d686b3 fed12823 fec12623 116b7
  //   60068693 fe012223 ff314203 fe4102a3 fef14203 fe410223 fe412203 468233 24203 fe4105a3 ff214203
  //   fe4102a3 fee14203 fe410223 fe412203 468233 24203 fe410523 ff114203 fe4102a3 fed14203 fe410223
  //   fe412203 468233 24203 fe4104a3 ff014203 fe4102a3 fec14203 fe410223 fe412203 468233 24203 fe410423
  //   fe812683 4a503 fe012823 fee10923 fee12423 fe914203 fe4109a3 ff012703 fee12823 fed12623 11737
  //   60070713 fe012223 ff314203 fe4102a3 fef14203 fe410223 fe412203 470233 24203 fe4105a3 ff214203
  //   fe4102a3 fee14203 fe410223 fe412203 470233 24203 fe410523 ff114203 fe4102a3 fed14203 fe410223
  //   fe412203 470233 24203 fe4104a3 ff014203 fe4102a3 fec14203 fe410223 fe412203 470233 24203 fe410423
  //   fe812703 fe012823 fef109a3 ff012783 fef12823 fee12623 117b7 60078793 fe012223 ff314203 fe4102a3
  //   fef14203 fe410223 fe412203 478233 24203 fe4105a3 ff214203 fe4102a3 fee14203 fe410223 fe412203 478233
  //   24203 fe410523 ff114203 fe4102a3 fed14203 fe410223 fe412203 478233 24203 fe4104a3 ff014203 fe4102a3
  //   fec14203 fe410223 fe412203 478233 24203 fe410423 fe812783 fe312a23 fef12423 31237 50020213 feb14183
  //   4181b3 1c183 fe3103a3 fea14183 4181b3 1c183 fe310323 fe914183 4181b3 1c183 fe3102a3 fe814183 4181b3
  //   1c183 fe310223 ff412183 fe412203 450533 150513 fea12823 fe812e23 1437 40840413 ff014183 3401b3 1c183
  //   ff114203 440233 24203 4181b3 ff214203 440233 24203 4181b3 ff314203 440233 24203 4181b3 1237 400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
endmodule

module my_decoder (
  input  [31:0] instruction,
  output [6:0] opcode,
  output [4:0] rd,
  output [2:0] funct3,
  output [4:0] rs1,
  output [4:0] rs2,
  output [6:0] funct7
);


  assign funct3 = instruction[14:12];
  assign funct7 = instruction[31:25];
  assign opcode = instruction[6:0];
  assign rd = instruction[11:7];
  assign rs1 = instruction[19:15];
  assign rs2 = instruction[24:20];
endmodule

module which_type (
  input  [6:0] opcode,
  output r_type,
  output i_type,
  output s_type,
  output u_type
);

  wire and_2_out, and_3_out, and_4_out;

  and and_1 (r_type, opcode[0], opcode[1], ~opcode[2], ~opcode[3], opcode[4], opcode[5], ~opcode[6]);  // AND_Gate
  and and_2 (and_2_out, opcode[0], opcode[1], ~opcode[2], ~opcode[3], opcode[4], ~opcode[5], ~opcode[6]);  // AND_Gate
  and and_3 (and_3_out, opcode[0], opcode[1], ~opcode[2], ~opcode[3], ~opcode[4], ~opcode[5], ~opcode[6]);  // AND_Gate
  and and_4 (and_4_out, opcode[0], opcode[1], opcode[2], ~opcode[3], ~opcode[4], opcode[5], opcode[6]);  // AND_Gate
  and and_5 (s_type, opcode[0], opcode[1], ~opcode[2], ~opcode[3], ~opcode[4], opcode[5], ~opcode[6]);  // AND_Gate
  and and_6 (u_type, opcode[0], opcode[1], opcode[2], ~opcode[3], opcode[4], opcode[5], ~opcode[6]);  // AND_Gate
  or or_1 (i_type, and_2_out, and_3_out, and_4_out);
endmodule

module alu (
  input  [31:0] a,
  input  [31:0] b,
  output [31:0] y
);

  Adder #(.width(32)) adder_1 (.a(a), .b(b), .out(y));  // open: cin, cout
endmodule

module register_file (
  input  [4:0] rs1_addr,
  input  [4:0] rs2_addr,
  input  [4:0] rd_addr,
  input  reg_write,
  input  [31:0] rd_data,
  input  clk,
  input  rst,
  output [31:0] rs1_val,
  output [31:0] rs2_val,
  output [31:0] reg0_val,
  output [31:0] reg1_val,
  output [31:0] reg2_val,
  output [31:0] reg3_val,
  output [31:0] reg4_val,
  output [31:0] reg5_val,
  output [31:0] reg6_val,
  output [31:0] reg7_val,
  output [31:0] reg8_val,
  output [31:0] reg9_val,
  output [31:0] reg10_val,
  output [31:0] reg11_val,
  output [31:0] reg12_val,
  output [31:0] reg13_val,
  output [31:0] reg14_val,
  output [31:0] reg15_val
);

  wire reg_0_out, reg_1_out, reg_2_out, reg_3_out, reg_4_out, reg_5_out, reg_6_out, reg_7_out, reg_8_out,
       reg_9_out, reg_10_out, reg_11_out, reg_12_out, reg_13_out, reg_14_out, reg_15_out;

  and reg_0 (reg_0_out, ~rd_addr[0], ~rd_addr[1], ~rd_addr[2], ~rd_addr[3], reg_write);  // AND_Gate
  and reg_1 (reg_1_out, rd_addr[0], ~rd_addr[1], ~rd_addr[2], ~rd_addr[3], reg_write);  // AND_Gate
  and reg_2 (reg_2_out, ~rd_addr[0], rd_addr[1], ~rd_addr[2], ~rd_addr[3], reg_write);  // AND_Gate
  and reg_3 (reg_3_out, rd_addr[0], rd_addr[1], ~rd_addr[2], ~rd_addr[3], reg_write);  // AND_Gate
  and reg_4 (reg_4_out, ~rd_addr[0], ~rd_addr[1], rd_addr[2], ~rd_addr[3], reg_write);  // AND_Gate
  and reg_5 (reg_5_out, rd_addr[0], ~rd_addr[1], rd_addr[2], ~rd_addr[3], reg_write);  // AND_Gate
  and reg_6 (reg_6_out, ~rd_addr[0], rd_addr[1], rd_addr[2], ~rd_addr[3], reg_write);  // AND_Gate
  and reg_7 (reg_7_out, rd_addr[0], rd_addr[1], rd_addr[2], ~rd_addr[3], reg_write);  // AND_Gate
  and reg_8 (reg_8_out, ~rd_addr[0], ~rd_addr[1], ~rd_addr[2], rd_addr[3], reg_write);  // AND_Gate
  and reg_9 (reg_9_out, rd_addr[0], ~rd_addr[1], ~rd_addr[2], rd_addr[3], reg_write);  // AND_Gate
  and reg_10 (reg_10_out, ~rd_addr[0], rd_addr[1], ~rd_addr[2], rd_addr[3], reg_write);  // AND_Gate
  and reg_11 (reg_11_out, rd_addr[0], rd_addr[1], ~rd_addr[2], rd_addr[3], reg_write);  // AND_Gate
  and reg_12 (reg_12_out, ~rd_addr[0], ~rd_addr[1], rd_addr[2], rd_addr[3], reg_write);  // AND_Gate
  and reg_13 (reg_13_out, rd_addr[0], ~rd_addr[1], rd_addr[2], rd_addr[3], reg_write);  // AND_Gate
  and reg_14 (reg_14_out, ~rd_addr[0], rd_addr[1], rd_addr[2], rd_addr[3], reg_write);  // AND_Gate
  and reg_15 (reg_15_out, rd_addr[0], rd_addr[1], rd_addr[2], rd_addr[3], reg_write);
  register_32bits register_32bits_1 (.D({32{1'b0}}), .enable(reg_0_out), .clk(clk), .rst(rst), .reg_out(reg0_val));
  register_32bits register_32bits_2 (.D(rd_data), .enable(reg_1_out), .clk(clk), .rst(rst), .reg_out(reg1_val));
  register_32bits register_32bits_3 (.D(rd_data), .enable(reg_2_out), .clk(clk), .rst(rst), .reg_out(reg2_val));
  register_32bits register_32bits_4 (.D(rd_data), .enable(reg_3_out), .clk(clk), .rst(rst), .reg_out(reg3_val));
  register_32bits register_32bits_5 (.D(rd_data), .enable(reg_4_out), .clk(clk), .rst(rst), .reg_out(reg4_val));
  register_32bits register_32bits_6 (.D(rd_data), .enable(reg_5_out), .clk(clk), .rst(rst), .reg_out(reg5_val));
  register_32bits register_32bits_7 (.D(rd_data), .enable(reg_6_out), .clk(clk), .rst(rst), .reg_out(reg6_val));
  register_32bits register_32bits_8 (.D(rd_data), .enable(reg_7_out), .clk(clk), .rst(rst), .reg_out(reg7_val));
  register_32bits register_32bits_9 (.D(rd_data), .enable(reg_8_out), .clk(clk), .rst(rst), .reg_out(reg8_val));
  register_32bits register_32bits_10 (.D(rd_data), .enable(reg_9_out), .clk(clk), .rst(rst), .reg_out(reg9_val));
  register_32bits register_32bits_11 (.D(rd_data), .enable(reg_10_out), .clk(clk), .rst(rst), .reg_out(reg10_val));
  register_32bits register_32bits_12 (.D(rd_data), .enable(reg_11_out), .clk(clk), .rst(rst), .reg_out(reg11_val));
  register_32bits register_32bits_13 (.D(rd_data), .enable(reg_12_out), .clk(clk), .rst(rst), .reg_out(reg12_val));
  register_32bits register_32bits_14 (.D(rd_data), .enable(reg_13_out), .clk(clk), .rst(rst), .reg_out(reg13_val));
  register_32bits register_32bits_15 (.D(rd_data), .enable(reg_14_out), .clk(clk), .rst(rst), .reg_out(reg14_val));
  register_32bits register_32bits_16 (.D(rd_data), .enable(reg_15_out), .clk(clk), .rst(rst), .reg_out(reg15_val));
  Multiplexer #(.select(4), .width(32)) multiplexer_1 (
    .in0(reg0_val), .in1(reg1_val), .in2(reg2_val), .in3(reg3_val), .in4(reg4_val), .in5(reg5_val),
    .in6(reg6_val), .in7(reg7_val), .in8(reg8_val), .in9(reg9_val), .in10(reg10_val), .in11(reg11_val),
    .in12(reg12_val), .in13(reg13_val), .in14(reg14_val), .in15(reg15_val), .out(rs1_val), .sel(rs1_addr[3:0]));
  Multiplexer #(.select(4), .width(32)) multiplexer_2 (
    .in0(reg0_val), .in1(reg1_val), .in2(reg2_val), .in3(reg3_val), .in4(reg4_val), .in5(reg5_val),
    .in6(reg6_val), .in7(reg7_val), .in8(reg8_val), .in9(reg9_val), .in10(reg10_val), .in11(reg11_val),
    .in12(reg12_val), .in13(reg13_val), .in14(reg14_val), .in15(reg15_val), .out(rs2_val), .sel(rs2_addr[3:0]));
endmodule

module immediate_generator (
  input  illegal,
  input  r_type,
  input  i_type,
  input  [31:0] instruction,
  input  s_type,
  input  u_type,
  output [31:0] imm
);

  wire [1:0] or_1_out;

  or or_1 (or_1_out[0], illegal, s_type);
  or or_2 (or_1_out[1], illegal, u_type);
  Multiplexer #(.select(2), .width(32)) multiplexer_1 (
    .in0({{21{instruction[31]}}, instruction[30:20]}),
    .in1({{21{instruction[31]}}, instruction[30:25], instruction[11:7]}),
    .in2({instruction[31:12], {12{1'b0}}}), .in3({32{1'b0}}), .out(imm), .sel(or_1_out));
endmodule

module which_instruction (
  input  [6:0] opcode,
  input  [2:0] funct3,
  input  [6:0] funct7,
  output add,
  output addi,
  output lui,
  output lw,
  output lbu,
  output sw,
  output sb,
  output jalr,
  output illegal
);

  wire comparator_1_eq, comparator_2_eq, comparator_3_eq, comparator_4_eq, comparator_6_eq, comparator_7_eq,
       comparator_8_eq, comparator_9_eq, comparator_10_eq;

  Comparator #(.width(7)) comparator_1 (.a(opcode), .b(7'b0110011), .eq(comparator_1_eq));  // open: gt, lt
  Comparator #(.width(7)) comparator_2 (.a(opcode), .b(7'b0010011), .eq(comparator_2_eq));  // open: gt, lt
  Comparator #(.width(7)) comparator_3 (.a(opcode), .b(7'b0000011), .eq(comparator_3_eq));  // open: gt, lt
  Comparator #(.width(7)) comparator_4 (.a(opcode), .b(7'b0100011), .eq(comparator_4_eq));  // open: gt, lt
  Comparator #(.width(7)) comparator_5 (.a(opcode), .b(7'b0110111), .eq(lui));  // open: gt, lt
  Comparator #(.width(7)) comparator_6 (.a(opcode), .b(7'b1100111), .eq(comparator_6_eq));  // open: gt, lt
  Comparator #(.width(3)) comparator_7 (.a(funct3), .b(3'b000), .eq(comparator_7_eq));  // open: gt, lt
  Comparator #(.width(3)) comparator_8 (.a(funct3), .b(3'b010), .eq(comparator_8_eq));  // open: gt, lt
  Comparator #(.width(3)) comparator_9 (.a(funct3), .b(3'b100), .eq(comparator_9_eq));  // open: gt, lt
  Comparator #(.width(7)) comparator_10 (.a(funct7), .b({7{1'b0}}), .eq(comparator_10_eq));  // open: gt, lt
  and and_1 (add, comparator_1_eq, comparator_7_eq, comparator_10_eq);
  and and_2 (addi, comparator_2_eq, comparator_7_eq);
  and and_3 (lw, comparator_3_eq, comparator_8_eq);
  and and_4 (lbu, comparator_3_eq, comparator_9_eq);
  and and_5 (sw, comparator_4_eq, comparator_8_eq);
  and and_6 (sb, comparator_7_eq, comparator_4_eq);
  and and_7 (jalr, comparator_6_eq, comparator_7_eq);
  nor nor_1 (illegal, add, addi, lui, lw, lbu, sw, sb, jalr);
endmodule

module b_mux (
  input  [31:0] rs2_val,
  input  [31:0] imm,
  input  addi,
  input  lw,
  input  lbu,
  input  sw,
  input  sb,
  input  jalr,
  output [31:0] b
);

  wire or_1_out;

  or or_1 (or_1_out, addi, lw, lbu, sw, sb, jalr);
  Multiplexer #(.width(32)) multiplexer_1 (.in0(rs2_val), .in1(imm), .out(b), .sel(or_1_out));
endmodule

module data_memory (
  input  [31:0] addr,
  input  [31:0] write_data,
  input  sw,
  input  sb,
  input  lw,
  input  lbu,
  input  clk,
  output [31:0] read_data
);

  wire s0_out, s1_out, s2_out, s3_out, sRAM0_out, sRAM1_out, sRAM2_out, sRAM3_out, w0_out, w1_out, w2_out,
       w3_out, wRAM0_out, wRAM1_out, wRAM2_out, wRAM3_out;
  wire [7:0] multiplexer_1_out, ram_1_dout, ram_2_dout, ram_3_dout, ram_4_dout;

  and sRAM0 (sRAM0_out, ~addr[0], ~addr[1], sb);  // AND_Gate
  and sRAM1 (sRAM1_out, addr[0], ~addr[1], sb);  // AND_Gate
  and sRAM2 (sRAM2_out, ~addr[0], addr[1], sb);  // AND_Gate
  and sRAM3 (sRAM3_out, addr[0], addr[1], sb);
  and wRAM0 (wRAM0_out, ~addr[0], ~addr[1], lbu);  // AND_Gate
  and wRAM1 (wRAM1_out, addr[0], ~addr[1], lbu);  // AND_Gate
  and wRAM2 (wRAM2_out, ~addr[0], addr[1], lbu);  // AND_Gate
  and wRAM3 (wRAM3_out, addr[0], addr[1], lbu);
  or s0 (s0_out, sRAM0_out, sw);
  or s1 (s1_out, sRAM1_out, sw);
  or s2 (s2_out, sRAM2_out, sw);
  or s3 (s3_out, sRAM3_out, sw);
  or w0 (w0_out, wRAM0_out, lw);
  or w1 (w1_out, wRAM1_out, lw);
  or w2 (w2_out, wRAM2_out, lw);
  or w3 (w3_out, wRAM3_out, lw);
  RAM #(.addrWidth(24)) ram_1 (
    .addr(addr[25:2]), .we(s0_out), .oe(w0_out), .clk(clk), .din(write_data[7:0]), .dout(ram_1_dout));
  RAM #(.addrWidth(24)) ram_2 (
    .addr(addr[25:2]), .we(s1_out), .oe(w1_out), .clk(clk), .din(write_data[15:8]), .dout(ram_2_dout));
  RAM #(.addrWidth(24)) ram_3 (
    .addr(addr[25:2]), .we(s2_out), .oe(w2_out), .clk(clk), .din(write_data[23:16]), .dout(ram_3_dout));
  RAM #(.addrWidth(24)) ram_4 (
    .addr(addr[25:2]), .we(s3_out), .oe(w3_out), .clk(clk), .din(write_data[31:24]), .dout(ram_4_dout));
  Multiplexer #(.select(2), .width(8)) multiplexer_1 (
    .in0(ram_1_dout), .in1(ram_2_dout), .in2(ram_3_dout), .in3(ram_4_dout), .out(multiplexer_1_out),
    .sel(addr[1:0]));
  Multiplexer #(.width(32)) multiplexer_2 (
    .in0({{24{1'b0}}, multiplexer_1_out}), .in1({ram_4_dout, ram_3_dout, ram_2_dout, ram_1_dout}),
    .out(read_data), .sel(lw));
endmodule

module writeback_mux (
  input  [31:0] y,
  input  [31:0] imm,
  input  [31:0] read_data,
  input  [31:0] pc_plus_4,
  input  lw,
  input  lbu,
  input  lui,
  input  jalr,
  output [31:0] rd_data
);

  wire mem_sel_out;
  wire [31:0] multiplexer_1_out, multiplexer_2_out;

  or mem_sel (mem_sel_out, lw, lbu);
  Multiplexer #(.width(32)) multiplexer_1 (.in0(y), .in1(read_data), .out(multiplexer_1_out), .sel(mem_sel_out));
  Multiplexer #(.width(32)) multiplexer_2 (.in0(multiplexer_1_out), .in1(imm), .out(multiplexer_2_out), .sel(lui));
  Multiplexer #(.width(32)) multiplexer_3 (.in0(multiplexer_2_out), .in1(pc_plus_4), .out(rd_data), .sel(jalr));
endmodule

module next_pc (
  input  [31:0] pc_plus_4,
  input  [31:0] y,
  input  jalr,
  output [31:0] pc_next
);

  wire [3:0] and_1_out, and_2_out, and_3_out, and_4_out, and_5_out, and_6_out, and_7_out, and_8_out;

  assign and_1_out = y[3:0] & 4'b1100;  // AND_Gate and_1, 4 bits wide
  assign and_2_out = y[7:4] & 4'b1111;  // AND_Gate and_2, 4 bits wide
  assign and_3_out = y[11:8] & 4'b1111;  // AND_Gate and_3, 4 bits wide
  assign and_4_out = y[15:12] & 4'b1111;  // AND_Gate and_4, 4 bits wide
  assign and_5_out = y[19:16] & 4'b1111;  // AND_Gate and_5, 4 bits wide
  assign and_6_out = y[23:20] & 4'b1111;  // AND_Gate and_6, 4 bits wide
  assign and_7_out = y[27:24] & 4'b1111;  // AND_Gate and_7, 4 bits wide
  assign and_8_out = y[31:28] & 4'b1111;  // AND_Gate and_8, 4 bits wide
  Multiplexer #(.width(32)) multiplexer_1 (
    .in0(pc_plus_4),
    .in1({and_8_out, and_7_out, and_6_out, and_5_out, and_4_out, and_3_out, and_2_out, and_1_out}),
    .out(pc_next), .sel(jalr));
endmodule

module pc_plus_4 (
  input  [31:0] pc,
  output [31:0] pc_plus_4_out
);

  Adder #(.width(32)) adder_1 (.a(pc), .b(32'h4), .out(pc_plus_4_out));  // open: cin, cout
endmodule

module reg_write_enabler (
  input  add,
  input  addi,
  input  lui,
  input  lw,
  input  lbu,
  input  jalr,
  input  illegal,
  output reg_write
);

  wire or_1_out;

  or or_1 (or_1_out, add, addi, lui, lw, lbu, jalr);
  and and_1 (reg_write, or_1_out, ~illegal);  // AND_Gate
endmodule

module pc_enabler (
  input  clk,
  input  [31:0] x,
  output pc_enabler_out
);

  wire comparator_1_eq, multiplexer_1_out;
  wire [31:0] counter_1_q;

  Counter #(.max('hffffffff), .width(32)) counter_1 (
    .clk(multiplexer_1_out), .Q(counter_1_q));  // open: clr, load, up, count, D, carry
  Multiplexer multiplexer_1 (.in0(clk), .in1(1'b0), .out(multiplexer_1_out), .sel(comparator_1_eq));
  Comparator #(.width(32)) comparator_1 (.a(counter_1_q), .b(x), .eq(comparator_1_eq));  // open: gt, lt
  Multiplexer multiplexer_2 (.in0(1'b1), .in1(1'b0), .out(pc_enabler_out), .sel(comparator_1_eq));
endmodule
