// Logisim project zhan_design.circ as structural Verilog: 10 circuits, main circuit main
module main (
  input  rst,
  output [7:0] out_2,
  output [3:0] out_3,
  output [7:0] out_4,
  output [7:0] out_5,
  output [7:0] out_6,
  output [7:0] out_7,
  output [7:0] out_8
);

  wire alu_1_equal, clock_1_out, reg_enabler_1_reg1_en, reg_enabler_1_reg2_en, reg_enabler_1_reg3_en,
       reg_enabler_1_reg4_en, which_type_1_add, which_type_1_bne, which_type_1_empty_inst, which_type_1_li;
  wire [1:0] my_decoder_1_op, my_decoder_1_rd, my_decoder_1_rs1, my_decoder_1_rs2;
  wire [3:0] my_decoder_1_addr, my_decoder_1_imm, pc_changer_1_changer_out;
  wire [7:0] selector_1_a, selector_1_b, selector_1_reg0_out;

  Reg_enabler reg_enabler_1 (
    .rd(my_decoder_1_rd), .bne(which_type_1_bne), .empty_inst(which_type_1_empty_inst),
    .reg1_en(reg_enabler_1_reg1_en), .reg2_en(reg_enabler_1_reg2_en), .reg3_en(reg_enabler_1_reg3_en),
    .reg4_en(reg_enabler_1_reg4_en));
  Clock clock_1 (.out(clock_1_out));
  Regx4 regx4_1 (.D(out_8), .enable(reg_enabler_1_reg1_en), .clk(clock_1_out), .rst(rst), .reg_out(out_2));
  Regx4 regx4_2 (.D(out_8), .enable(reg_enabler_1_reg2_en), .clk(clock_1_out), .rst(rst), .reg_out(out_5));
  Regx4 regx4_3 (.D(out_8), .enable(reg_enabler_1_reg3_en), .clk(clock_1_out), .rst(rst), .reg_out(out_6));
  Regx4 regx4_4 (.D(out_8), .enable(reg_enabler_1_reg4_en), .clk(clock_1_out), .rst(rst), .reg_out(out_7));
  PC pc_1 (.D(pc_changer_1_changer_out), .enable(1'b1), .clk(clock_1_out), .rst(rst), .out_5(out_3));
  Selector selector_1 (
    .rs1(my_decoder_1_rs1), .rs2(my_decoder_1_rs2), .reg0_in(out_2), .reg1_in(out_5), .reg2_in(out_6),
    .reg3_in(out_7), .A(selector_1_a), .B(selector_1_b), .reg0_out(selector_1_reg0_out));
  Instruction_memory instruction_memory_1 (.sel(out_3), .instruction_out(out_4));
  ALU alu_1 (
    .A(selector_1_a), .B(selector_1_b), .imm(my_decoder_1_imm), .reg0_val(selector_1_reg0_out),
    .add(which_type_1_add), .ALU_out(out_8), .equal(alu_1_equal));
  my_decoder my_decoder_1 (
    .D(out_4), .op(my_decoder_1_op), .rd(my_decoder_1_rd), .rs1(my_decoder_1_rs1), .rs2(my_decoder_1_rs2),
    .addr(my_decoder_1_addr), .imm(my_decoder_1_imm));
  which_type which_type_1 (
    .op(my_decoder_1_op), .add(which_type_1_add), .li(which_type_1_li), .bne(which_type_1_bne),
    .empty_inst(which_type_1_empty_inst));
  PC_changer pc_changer_1 (
    .PC(out_3), .add(which_type_1_add), .li(which_type_1_li), .addr(my_decoder_1_addr), .equal(alu_1_equal),
    .empty_inst(which_type_1_empty_inst), .changer_out(pc_changer_1_changer_out));
endmodule

module PC (
  input  [3:0] D,
  input  enable,
  input  clk,
  input  rst,
  output [3:0] out_5
);

  Register #(.width(4)) register_1 (.D(D), .en(enable), .clk(clk), .Q(out_5), .clr(rst));
endmodule

module Instruction_memory (
  input  [3:0] sel,
  output [7:0] instruction_out
);

  Multiplexer #(.select(4), .width(8)) multiplexer_1 (
    .in0(8'h8a), .in1(8'h90), .in2(8'ha0), .in3(8'hb1), .in4(8'h17), .in5(8'h29), .in6(8'hd1), .in7(8'hdf),
    .in8({8{1'b0}}), .in9({8{1'b0}}), .in10({8{1'b0}}), .in11({8{1'b0}}), .in12({8{1'b0}}), .in13({8{1'b0}}),
    .in14({8{1'b0}}), .in15({8{1'b0}}), .out(instruction_out), .sel(sel));
endmodule

module my_decoder (
  input  [7:0] D,
  output [1:0] op,
  output [1:0] rd,
  output [1:0] rs1,
  output [1:0] rs2,
  output [3:0] addr,
  output [3:0] imm
);


  assign addr = D[5:2];
  assign imm = D[3:0];
  assign op = D[7:6];
  assign rd = D[5:4];
  assign rs1 = D[3:2];
  assign rs2 = D[1:0];
endmodule

module which_type (
  input  [1:0] op,
  output add,
  output li,
  output bne,
  output empty_inst
);

  and and_1 (add, ~op[0], ~op[1]);  // AND_Gate
  and and_2 (li, ~op[0], op[1]);  // AND_Gate
  and and_3 (bne, op[0], op[1]);
  and and_4 (empty_inst, op[0], ~op[1]);  // AND_Gate
endmodule

module ALU (
  input  [7:0] A,
  input  [7:0] B,
  input  [3:0] imm,
  input  [7:0] reg0_val,
  input  add,
  output [7:0] ALU_out,
  output equal
);

  wire not_1_out;
  wire [7:0] adder_1_out;

  Adder adder_1 (.a(A), .b(B), .out(adder_1_out));  // open: cin, cout
  Comparator comparator_1 (.a(B), .b(reg0_val), .eq(equal));  // open: gt, lt
  not not_1 (not_1_out, add);
  Multiplexer #(.width(8)) multiplexer_1 (.in0(adder_1_out), .in1({4'b0000, imm}), .out(ALU_out), .sel(not_1_out));
endmodule

module Regx4 (
  input  [7:0] D,
  input  enable,
  input  clk,
  input  rst,
  output [7:0] reg_out
);

  Register register_1 (.D(D), .en(enable), .clk(clk), .Q(reg_out), .clr(rst));
endmodule

module PC_changer (
  input  [3:0] PC,
  input  add,
  input  li,
  input  [3:0] addr,
  input  equal,
  input  empty_inst,
  output [3:0] changer_out
);

  wire nor_1_out, not_1_out;
  wire [3:0] adder_1_out, multiplexer_1_out, multiplexer_2_out;

  not not_1 (not_1_out, equal);
  Adder #(.width(4)) adder_1 (.a(PC), .b(4'b0001), .out(adder_1_out));  // open: cin, cout
  nor nor_1 (nor_1_out, add, li);
  Multiplexer #(.width(4)) multiplexer_1 (.in0(adder_1_out), .in1(addr), .out(multiplexer_1_out), .sel(not_1_out));
  Multiplexer #(.width(4)) multiplexer_2 (
    .in0(adder_1_out), .in1(multiplexer_1_out), .out(multiplexer_2_out), .sel(nor_1_out));
  Multiplexer #(.width(4)) multiplexer_3 (
    .in0(multiplexer_2_out), .in1(adder_1_out), .out(changer_out), .sel(empty_inst));
endmodule

module Reg_enabler (
  input  [1:0] rd,
  input  bne,
  input  empty_inst,
  output reg1_en,
  output reg2_en,
  output reg3_en,
  output reg4_en
);

  and and_1 (reg1_en, ~rd[0], ~rd[1], ~bne, ~empty_inst);  // AND_Gate
  and and_2 (reg2_en, rd[0], ~rd[1], ~bne, ~empty_inst);  // AND_Gate
  and and_3 (reg3_en, ~rd[0], rd[1], ~bne, ~empty_inst);  // AND_Gate
  and and_4 (reg4_en, rd[0], rd[1], ~bne, empty_inst);  // AND_Gate
endmodule

module Selector (
  input  [1:0] rs1,
  input  [1:0] rs2,
  input  [7:0] reg0_in,
  input  [7:0] reg1_in,
  input  [7:0] reg2_in,
  input  [7:0] reg3_in,
  output [7:0] A,
  output [7:0] B,
  output [7:0] reg0_out
);

  Multiplexer #(.select(2), .width(8)) multiplexer_1 (
    .in0(reg0_in), .in1(reg1_in), .in2(reg2_in), .in3(reg3_in), .out(A), .sel(rs1));
  Multiplexer #(.select(2), .width(8)) multiplexer_2 (
    .in0(reg0_in), .in1(reg1_in), .in2(reg2_in), .in3(reg3_in), .out(B), .sel(rs2));

  assign reg0_out = reg0_in;
endmodule
