// Logisim project osoc.circ as structural Verilog: 37 circuits, main circuit main
module main (
);

  wire clock_1_out, clock_2_out, decoder7seg_1_a, decoder7seg_1_b, decoder7seg_1_c, decoder7seg_1_d,
       decoder7seg_1_e, decoder7seg_1_f, decoder7seg_1_g, dipswitch_1_sw8;
  wire [3:0] adderx4_1_s, dipswitch_1_sw4, regx4_1_q;

  Button button_1 ();  // open: out
  Clock clock_1 (.out(clock_1_out));
  DipSwitch dipswitch_1 (
    .sw1(dipswitch_1_sw4[3]), .sw2(dipswitch_1_sw4[2]), .sw3(dipswitch_1_sw4[1]), .sw4(dipswitch_1_sw4[0]),
    .sw8(dipswitch_1_sw8));  // open: sw5, sw6, sw7
  Clock clock_2 (.out(clock_2_out));
  LED led_1 (.in(clock_2_out));
  Regx4 regx4_1 (.D(adderx4_1_s), .rst(dipswitch_1_sw8), .clk(clock_1_out), .Q(regx4_1_q));
  Adderx4 adderx4_1 (.A(regx4_1_q), .B(4'b0001), .S(adderx4_1_s));  // open: cin, C
  Decoder7seg decoder7seg_1 (
    .in_1(regx4_1_q), .a(decoder7seg_1_a), .b(decoder7seg_1_b), .c(decoder7seg_1_c), .d(decoder7seg_1_d),
    .e(decoder7seg_1_e), .f(decoder7seg_1_f), .g(decoder7seg_1_g));  // open: h
  _7_Segment_Display u_7_segment_display_1 (
    .g(decoder7seg_1_g), .f(decoder7seg_1_f), .a(decoder7seg_1_a), .b(decoder7seg_1_b), .e(decoder7seg_1_e),
    .d(decoder7seg_1_d), .c(decoder7seg_1_c));  // open: dp
endmodule

module SR_latch (
  input  R,
  input  S,
  output Q,
  output Q0
);

  nor nor_1 (Q, R, Q0);
  nor nor_2 (Q0, Q, S);
endmodule

module D_latch (
  input  D,
  input  WE,
  output Q,
  output out_4
);

  wire and_1_out, and_2_out, not_1_out;

  not not_1 (not_1_out, D);
  and and_1 (and_1_out, not_1_out, WE);
  and and_2 (and_2_out, WE, D);
  SR_latch sr_latch_1 (.R(and_1_out), .S(and_2_out), .Q(Q), .Q0(out_4));
endmodule

module Decoder7seg (
  input  [3:0] in_1,
  output a,
  output b,
  output c,
  output d,
  output e,
  output f,
  output g,
  output h
);

  wire or_1_out, or_2_out, or_3_out, or_4_out, or_5_out, or_6_out;
  wire [15:0] decoder4_16_1_out_2;

  Decoder4_16 decoder4_16_1 (.in_1(in_1), .out_2(decoder4_16_1_out_2));
  or or_1 (or_1_out, decoder4_16_1_out_2[15], decoder4_16_1_out_2[14], decoder4_16_1_out_2[12], decoder4_16_1_out_2[10], decoder4_16_1_out_2[9], decoder4_16_1_out_2[8], decoder4_16_1_out_2[7], decoder4_16_1_out_2[6], decoder4_16_1_out_2[5], decoder4_16_1_out_2[3], decoder4_16_1_out_2[2]);
  or or_2 (or_2_out, decoder4_16_1_out_2[13], decoder4_16_1_out_2[10], decoder4_16_1_out_2[9], decoder4_16_1_out_2[8], decoder4_16_1_out_2[7], decoder4_16_1_out_2[4], decoder4_16_1_out_2[3], decoder4_16_1_out_2[2], decoder4_16_1_out_2[1]);
  or or_3 (or_3_out, decoder4_16_1_out_2[13], decoder4_16_1_out_2[11], decoder4_16_1_out_2[10], decoder4_16_1_out_2[9], decoder4_16_1_out_2[8], decoder4_16_1_out_2[7], decoder4_16_1_out_2[6], decoder4_16_1_out_2[5], decoder4_16_1_out_2[4], decoder4_16_1_out_2[3], decoder4_16_1_out_2[1]);
  or or_4 (or_4_out, decoder4_16_1_out_2[14], decoder4_16_1_out_2[13], decoder4_16_1_out_2[12], decoder4_16_1_out_2[11], decoder4_16_1_out_2[9], decoder4_16_1_out_2[8], decoder4_16_1_out_2[6], decoder4_16_1_out_2[5], decoder4_16_1_out_2[3], decoder4_16_1_out_2[2]);
  or or_5 (or_5_out, decoder4_16_1_out_2[15], decoder4_16_1_out_2[14], decoder4_16_1_out_2[13], decoder4_16_1_out_2[12], decoder4_16_1_out_2[11], decoder4_16_1_out_2[10], decoder4_16_1_out_2[8], decoder4_16_1_out_2[6], decoder4_16_1_out_2[2]);
  or or_6 (or_6_out, decoder4_16_1_out_2[15], decoder4_16_1_out_2[14], decoder4_16_1_out_2[12], decoder4_16_1_out_2[11], decoder4_16_1_out_2[10], decoder4_16_1_out_2[9], decoder4_16_1_out_2[8], decoder4_16_1_out_2[6], decoder4_16_1_out_2[5], decoder4_16_1_out_2[4]);
  or or_7 (g, decoder4_16_1_out_2[15], decoder4_16_1_out_2[14], decoder4_16_1_out_2[13], decoder4_16_1_out_2[11], decoder4_16_1_out_2[10], decoder4_16_1_out_2[9], decoder4_16_1_out_2[8], decoder4_16_1_out_2[6], decoder4_16_1_out_2[5], decoder4_16_1_out_2[4], decoder4_16_1_out_2[3], decoder4_16_1_out_2[2]);
  or or_8 (a, or_1_out, decoder4_16_1_out_2[0]);
  or or_9 (b, or_2_out, decoder4_16_1_out_2[0]);
  or or_10 (c, or_3_out, decoder4_16_1_out_2[0]);
  or or_11 (d, or_4_out, decoder4_16_1_out_2[0]);
  or or_12 (e, or_5_out, decoder4_16_1_out_2[0]);
  or or_13 (f, or_6_out, decoder4_16_1_out_2[0]);

  assign h = 1'b0;
endmodule

module Decoder2_4 (
  input  [1:0] in_1,
  output [3:0] out_2
);

  wire not_1_out, not_2_out;

  not not_1 (not_1_out, in_1[0]);
  not not_2 (not_2_out, in_1[1]);
  and and_1 (out_2[0], not_1_out, not_2_out);
  and and_2 (out_2[1], in_1[0], not_2_out);
  and and_3 (out_2[2], in_1[1], not_1_out);
  and and_4 (out_2[3], in_1[0], in_1[1]);
endmodule

module Decoder3_8 (
  input  [2:0] in_1,
  output [7:0] out_2
);

  wire [3:0] decoder2_4_1_out_2, not_1_out;

  Decoder2_4 decoder2_4_1 (.in_1(in_1[1:0]), .out_2(decoder2_4_1_out_2));
  assign not_1_out = ~{4{in_1[2]}};  // NOT_Gate not_1, 4 bits wide
  assign out_2[3:0] = decoder2_4_1_out_2 & not_1_out;  // AND_Gate and_1, 4 bits wide
  assign out_2[7:4] = decoder2_4_1_out_2 & {4{in_1[2]}};  // AND_Gate and_2, 4 bits wide
endmodule

module Decoder4_16 (
  input  [3:0] in_1,
  output [15:0] out_2
);

  wire [7:0] decoder3_8_1_out_2, not_1_out;

  Decoder3_8 decoder3_8_1 (.in_1(in_1[2:0]), .out_2(decoder3_8_1_out_2));
  assign not_1_out = ~{8{in_1[3]}};  // NOT_Gate not_1, 8 bits wide
  assign out_2[7:0] = decoder3_8_1_out_2 & not_1_out;  // AND_Gate and_1, 8 bits wide
  assign out_2[15:8] = decoder3_8_1_out_2 & {8{in_1[3]}};  // AND_Gate and_2, 8 bits wide
endmodule

module MUX2to1x1 (
  input  S,
  input  D0,
  input  D1,
  output Y
);

  wire and_1_out, and_2_out, not_1_out;

  not not_1 (not_1_out, S);
  and and_1 (and_1_out, not_1_out, D0);
  and and_2 (and_2_out, S, D1);
  or or_1 (Y, and_1_out, and_2_out);
endmodule

module MUX2to1x2 (
  input  S,
  input  [1:0] D0,
  input  [1:0] D1,
  output [1:0] Y
);

  MUX2to1x1 mux2to1x1_1 (.S(S), .D0(D0[0]), .D1(D1[0]), .Y(Y[0]));
  MUX2to1x1 mux2to1x1_2 (.S(S), .D0(D0[1]), .D1(D1[1]), .Y(Y[1]));
endmodule

module MUX2to1x4 (
  input  S,
  input  [3:0] D0,
  input  [3:0] D1,
  output [3:0] Y
);

  MUX2to1x1 mux2to1x1_1 (.S(S), .D0(D0[0]), .D1(D1[0]), .Y(Y[0]));
  MUX2to1x1 mux2to1x1_2 (.S(S), .D0(D0[1]), .D1(D1[1]), .Y(Y[1]));
  MUX2to1x1 mux2to1x1_3 (.S(S), .D0(D0[2]), .D1(D1[2]), .Y(Y[2]));
  MUX2to1x1 mux2to1x1_4 (.S(S), .D0(D0[3]), .D1(D1[3]), .Y(Y[3]));
endmodule

module MUX2to1x8 (
  input  S,
  input  [7:0] D0,
  input  [7:0] D1,
  output [7:0] Y
);

  MUX2to1x4 mux2to1x4_1 (.S(S), .D0(D0[3:0]), .D1(D1[3:0]), .Y(Y[3:0]));
  MUX2to1x4 mux2to1x4_2 (.S(S), .D0(D0[7:4]), .D1(D1[7:4]), .Y(Y[7:4]));
endmodule

module MUX4to1x8 (
  input  [1:0] S,
  input  [7:0] D0,
  input  [7:0] D1,
  input  [7:0] D2,
  input  [7:0] D3,
  output [7:0] Y
);

  wire [7:0] mux2to1x8_1_y, mux2to1x8_2_y;

  MUX2to1x8 mux2to1x8_1 (.S(S[0]), .D0(D0), .D1(D1), .Y(mux2to1x8_1_y));
  MUX2to1x8 mux2to1x8_2 (.S(S[0]), .D0(D2), .D1(D3), .Y(mux2to1x8_2_y));
  MUX2to1x8 mux2to1x8_3 (.S(S[1]), .D0(mux2to1x8_1_y), .D1(mux2to1x8_2_y), .Y(Y));
endmodule

module MUX8to1x8 (
  input  [2:0] S,
  input  [7:0] D0,
  input  [7:0] D1,
  input  [7:0] D2,
  input  [7:0] D3,
  input  [7:0] D4,
  input  [7:0] D5,
  input  [7:0] D6,
  input  [7:0] D7,
  output [7:0] Y
);

  wire [7:0] mux4to1x8_1_y, mux4to1x8_2_y;

  MUX4to1x8 mux4to1x8_1 (.S(S[1:0]), .D0(D0), .D1(D1), .D2(D2), .D3(D3), .Y(mux4to1x8_1_y));
  MUX4to1x8 mux4to1x8_2 (.S(S[1:0]), .D0(D4), .D1(D5), .D2(D6), .D3(D7), .Y(mux4to1x8_2_y));
  MUX2to1x8 mux2to1x8_1 (.S(S[2]), .D0(mux4to1x8_1_y), .D1(mux4to1x8_2_y), .Y(Y));
endmodule

module Cmpx4 (
  input  [3:0] A,
  input  [3:0] B,
  output eq
);

  wire or_1_out;
  wire [3:0] xor_1_out;

  assign xor_1_out = A ^ B;  // XOR_Gate xor_1, 4 bits wide
  or or_1 (or_1_out, xor_1_out[0], xor_1_out[1], xor_1_out[2], xor_1_out[3]);
  not not_1 (eq, or_1_out);
endmodule

module Cmpx8 (
  input  [7:0] A,
  input  [7:0] B,
  output eq
);

  wire cmpx4_1_eq, cmpx4_2_eq;

  Cmpx4 cmpx4_1 (.A(A[3:0]), .B(B[3:0]), .eq(cmpx4_1_eq));
  Cmpx4 cmpx4_2 (.A(A[7:4]), .B(B[7:4]), .eq(cmpx4_2_eq));
  and and_1 (eq, cmpx4_1_eq, cmpx4_2_eq);
endmodule

module HA (
  input  A,
  input  B,
  output S,
  output C
);

  xor xor_1 (S, A, B);
  and and_1 (C, A, B);
endmodule

module FA (
  input  A,
  input  B,
  input  Cin,
  output S,
  output Cout
);

  wire ha_1_c, ha_1_s, ha_2_c;

  HA ha_1 (.A(A), .B(B), .S(ha_1_s), .C(ha_1_c));
  HA ha_2 (.A(ha_1_s), .B(Cin), .S(S), .C(ha_2_c));
  or or_1 (Cout, ha_1_c, ha_2_c);
endmodule

module Adderx4 (
  input  [3:0] A,
  input  [3:0] B,
  input  cin,
  output [3:0] S,
  output C
);

  wire fa_1_cout, fa_2_cout, fa_3_cout;

  FA fa_1 (.A(A[0]), .B(B[0]), .Cin(cin), .S(S[0]), .Cout(fa_1_cout));
  FA fa_2 (.A(A[1]), .B(B[1]), .Cin(fa_1_cout), .S(S[1]), .Cout(fa_2_cout));
  FA fa_3 (.A(A[2]), .B(B[2]), .Cin(fa_2_cout), .S(S[2]), .Cout(fa_3_cout));
  FA fa_4 (.A(A[3]), .B(B[3]), .Cin(fa_3_cout), .S(S[3]), .Cout(C));
endmodule

module Adderx8 (
  input  [7:0] A,
  input  [7:0] B,
  input  cin,
  output [7:0] S,
  output C
);

  wire adderx4_1_c;

  Adderx4 adderx4_1 (.A(A[3:0]), .B(B[3:0]), .cin(cin), .S(S[3:0]), .C(adderx4_1_c));
  Adderx4 adderx4_2 (.A(A[7:4]), .B(B[7:4]), .cin(adderx4_1_c), .S(S[7:4]), .C(C));
endmodule

module D_latchx4 (
  input  WE,
  input  [3:0] D,
  output [3:0] Q
);

  D_latch d_latch_1 (.D(WE), .WE(D[0]), .Q(Q[0]));  // open: out_4
  D_latch d_latch_2 (.D(WE), .WE(D[1]), .Q(Q[1]));  // open: out_4
  D_latch d_latch_3 (.D(WE), .WE(D[2]), .Q(Q[2]));  // open: out_4
  D_latch d_latch_4 (.D(WE), .WE(D[3]), .Q(Q[3]));  // open: out_4
endmodule

module DFF (
  input  D,
  input  clk,
  output Q
);

  wire d_latch_1_q, not_1_out;

  not not_1 (not_1_out, clk);
  D_latch d_latch_1 (.D(D), .WE(clk), .Q(d_latch_1_q));  // open: out_4
  D_latch d_latch_2 (.D(d_latch_1_q), .WE(not_1_out), .Q(Q));  // open: out_4
endmodule

module DFFR (
  input  D,
  input  rst,
  input  clk,
  output Q
);

  wire mux2to1x1_1_y;

  MUX2to1x1 mux2to1x1_1 (.S(rst), .D0(D), .D1(1'b0), .Y(mux2to1x1_1_y));
  DFF dff_1 (.D(mux2to1x1_1_y), .clk(clk), .Q(Q));
endmodule

module Regx4 (
  input  [3:0] D,
  input  rst,
  input  clk,
  output [3:0] Q
);

  DFFR dffr_1 (.D(D[0]), .rst(rst), .clk(clk), .Q(Q[0]));
  DFFR dffr_2 (.D(D[1]), .rst(rst), .clk(clk), .Q(Q[1]));
  DFFR dffr_3 (.D(D[2]), .rst(rst), .clk(clk), .Q(Q[2]));
  DFFR dffr_4 (.D(D[3]), .rst(rst), .clk(clk), .Q(Q[3]));
endmodule

module Regx8 (
  input  [7:0] D,
  input  rst,
  input  clk,
  output [7:0] Q
);

  Regx4 regx4_1 (.D(D[3:0]), .rst(rst), .clk(clk), .Q(Q[3:0]));
  Regx4 regx4_2 (.D(D[7:4]), .rst(rst), .clk(clk), .Q(Q[7:4]));
endmodule

module RegEnx8 (
  input  [7:0] D,
  input  rst,
  input  clk,
  input  en,
  output [7:0] Q
);

  wire [7:0] mux2to1x8_1_y;

  MUX2to1x8 mux2to1x8_1 (.S(en), .D0(Q), .D1(D), .Y(mux2to1x8_1_y));
  Regx8 regx8_1 (.D(mux2to1x8_1_y), .rst(rst), .clk(clk), .Q(Q));
endmodule

module Counterx4 (
  input  rst,
  input  clk,
  input  en,
  output [3:0] Q
);

  wire [3:0] adderx4_1_s, mux2to1x4_1_y;

  Regx4 regx4_1 (.D(mux2to1x4_1_y), .rst(rst), .clk(clk), .Q(Q));
  Adderx4 adderx4_1 (.A(Q), .B(4'b0001), .cin(1'b0), .S(adderx4_1_s));  // open: C
  MUX2to1x4 mux2to1x4_1 (.S(en), .D0(Q), .D1(adderx4_1_s), .Y(mux2to1x4_1_y));
endmodule

module Counterx4_Top (
);

  wire clock_1_out, decoder7seg_1_a, decoder7seg_1_b, decoder7seg_1_c, decoder7seg_1_d, decoder7seg_1_e,
       decoder7seg_1_f, decoder7seg_1_g, dipswitch_1_sw8;
  wire [3:0] counterx4_1_q;

  Button button_1 ();  // open: out
  Clock clock_1 (.out(clock_1_out));
  DipSwitch dipswitch_1 (.sw8(dipswitch_1_sw8));  // open: sw1, sw2, sw3, sw4, sw5, sw6, sw7
  Counterx4 counterx4_1 (.rst(dipswitch_1_sw8), .clk(clock_1_out), .en(1'b1), .Q(counterx4_1_q));
  Decoder7seg decoder7seg_1 (
    .in_1(counterx4_1_q), .a(decoder7seg_1_a), .b(decoder7seg_1_b), .c(decoder7seg_1_c), .d(decoder7seg_1_d),
    .e(decoder7seg_1_e), .f(decoder7seg_1_f), .g(decoder7seg_1_g));  // open: h
  _7_Segment_Display u_7_segment_display_1 (
    .g(decoder7seg_1_g), .f(decoder7seg_1_f), .a(decoder7seg_1_a), .b(decoder7seg_1_b), .e(decoder7seg_1_e),
    .d(decoder7seg_1_d), .c(decoder7seg_1_c));  // open: dp
endmodule

module Sumx8_Top (
  output [7:0] out_1
);

  wire clock_1_out, dipswitch_1_sw8;
  wire [7:0] adderx8_1_s, adderx8_2_s, regx8_1_q;

  Clock clock_1 (.out(clock_1_out));
  DipSwitch dipswitch_1 (.sw8(dipswitch_1_sw8));  // open: sw1, sw2, sw3, sw4, sw5, sw6, sw7
  Regx8 regx8_1 (.D(adderx8_1_s), .rst(dipswitch_1_sw8), .clk(clock_1_out), .Q(regx8_1_q));
  Regx8 regx8_2 (.D(adderx8_2_s), .rst(dipswitch_1_sw8), .clk(clock_1_out), .Q(out_1));
  Adderx8 adderx8_1 (.A(regx8_1_q), .B(8'h1), .cin(1'b0), .S(adderx8_1_s));  // open: C
  Adderx8 adderx8_2 (.A(regx8_1_q), .B(out_1), .cin(1'b0), .S(adderx8_2_s));  // open: C
  // Probe on out_1
endmodule

module Clock_Top (
);

  wire and_1_out, clock_1_out, cmpx4_1_eq, cmpx4_2_eq, decoder7seg_1_a, decoder7seg_1_b, decoder7seg_1_c,
       decoder7seg_1_d, decoder7seg_1_e, decoder7seg_1_f, decoder7seg_1_g, decoder7seg_1_h, decoder7seg_2_a,
       decoder7seg_2_b, decoder7seg_2_c, decoder7seg_2_d, decoder7seg_2_e, decoder7seg_2_f, decoder7seg_2_g,
       decoder7seg_2_h, dipswitch_1_sw8, or_1_out, or_2_out;
  wire [3:0] counterx4_1_q, counterx4_2_q;

  DipSwitch dipswitch_1 (.sw8(dipswitch_1_sw8));  // open: sw1, sw2, sw3, sw4, sw5, sw6, sw7
  Clock clock_1 (.out(clock_1_out));
  or or_1 (or_1_out, cmpx4_1_eq, dipswitch_1_sw8);
  or or_2 (or_2_out, and_1_out, dipswitch_1_sw8);
  Counterx4 counterx4_1 (.rst(or_1_out), .clk(clock_1_out), .en(1'b1), .Q(counterx4_1_q));
  Counterx4 counterx4_2 (.rst(or_2_out), .clk(clock_1_out), .en(cmpx4_1_eq), .Q(counterx4_2_q));
  Cmpx4 cmpx4_1 (.A(counterx4_1_q), .B(4'b1001), .eq(cmpx4_1_eq));
  Cmpx4 cmpx4_2 (.A(counterx4_2_q), .B(4'b0101), .eq(cmpx4_2_eq));
  and and_1 (and_1_out, cmpx4_1_eq, cmpx4_2_eq);
  Decoder7seg decoder7seg_1 (
    .in_1(counterx4_1_q), .a(decoder7seg_1_a), .b(decoder7seg_1_b), .c(decoder7seg_1_c), .d(decoder7seg_1_d),
    .e(decoder7seg_1_e), .f(decoder7seg_1_f), .g(decoder7seg_1_g), .h(decoder7seg_1_h));
  Decoder7seg decoder7seg_2 (
    .in_1(counterx4_2_q), .a(decoder7seg_2_a), .b(decoder7seg_2_b), .c(decoder7seg_2_c), .d(decoder7seg_2_d),
    .e(decoder7seg_2_e), .f(decoder7seg_2_f), .g(decoder7seg_2_g), .h(decoder7seg_2_h));
  _7_Segment_Display u_7_segment_display_1 (
    .g(decoder7seg_1_g), .f(decoder7seg_1_f), .a(decoder7seg_1_a), .b(decoder7seg_1_b), .e(decoder7seg_1_e),
    .d(decoder7seg_1_d), .c(decoder7seg_1_c), .dp(decoder7seg_1_h));
  _7_Segment_Display u_7_segment_display_2 (
    .g(decoder7seg_2_g), .f(decoder7seg_2_f), .a(decoder7seg_2_a), .b(decoder7seg_2_b), .e(decoder7seg_2_e),
    .d(decoder7seg_2_d), .c(decoder7seg_2_c), .dp(decoder7seg_2_h));
endmodule

module RegFile4x8 (
  input  clk,
  input  [1:0] rs1,
  input  [1:0] rs2,
  input  [1:0] rd,
  input  wen,
  input  [7:0] wdata,
  output [7:0] rdata1,
  output [7:0] rdata2
);

  wire and_1_out, and_2_out, and_3_out, and_4_out;
  wire [3:0] decoder2_4_1_out_2;
  wire [7:0] regenx8_1_q, regenx8_2_q, regenx8_3_q, regenx8_4_q;

  Decoder2_4 decoder2_4_1 (.in_1(rd), .out_2(decoder2_4_1_out_2));
  and and_1 (and_1_out, decoder2_4_1_out_2[0], wen);
  and and_2 (and_2_out, decoder2_4_1_out_2[1], wen);
  and and_3 (and_3_out, decoder2_4_1_out_2[2], wen);
  and and_4 (and_4_out, decoder2_4_1_out_2[3], wen);
  // Probe on regenx8_1_q
  RegEnx8 regenx8_1 (.D(wdata), .rst(1'b0), .clk(clk), .en(and_1_out), .Q(regenx8_1_q));
  RegEnx8 regenx8_2 (.D(wdata), .rst(1'b0), .clk(clk), .en(and_2_out), .Q(regenx8_2_q));
  RegEnx8 regenx8_3 (.D(wdata), .rst(1'b0), .clk(clk), .en(and_3_out), .Q(regenx8_3_q));
  RegEnx8 regenx8_4 (.D(wdata), .rst(1'b0), .clk(clk), .en(and_4_out), .Q(regenx8_4_q));
  // Probe on regenx8_4_q
  // Probe on regenx8_2_q
  // Probe on regenx8_3_q
  MUX4to1x8 mux4to1x8_1 (.S(rs1), .D0(regenx8_1_q), .D1(regenx8_2_q), .D2(regenx8_3_q), .D3(regenx8_4_q), .Y(rdata1));
  MUX4to1x8 mux4to1x8_2 (.S(rs2), .D0(regenx8_1_q), .D1(regenx8_2_q), .D2(regenx8_3_q), .D3(regenx8_4_q), .Y(rdata2));
endmodule

module sISA_cpu_Top (
);

  wire and_1_out, and_2_out, clock_1_out, cmpx8_1_eq, dipswitch_1_sw1, not_1_out, not_2_out;
  wire [1:0] mux2to1x2_1_y;
  wire [3:0] adderx4_1_s, mux2to1x4_1_y, PC;
  wire [7:0] adderx8_1_s, mux2to1x8_1_y, mux8to1x8_1_y, regfile4x8_1_rdata1, regfile4x8_1_rdata2;

  Clock clock_1 (.out(clock_1_out));
  DipSwitch dipswitch_1 (.sw1(dipswitch_1_sw1));  // open: sw2, sw3, sw4, sw5, sw6, sw7, sw8
  Regx4 regx4_1 (.D(mux2to1x4_1_y), .rst(dipswitch_1_sw1), .clk(clock_1_out), .Q(PC));
  Adderx4 adderx4_1 (.A(PC), .B(4'b0001), .cin(1'b0), .S(adderx4_1_s));  // open: C
  MUX2to1x4 mux2to1x4_1 (.S(and_2_out), .D0(adderx4_1_s), .D1(mux8to1x8_1_y[5:2]), .Y(mux2to1x4_1_y));
  MUX8to1x8 mux8to1x8_1 (
    .S(PC[2:0]), .D0(8'h8a), .D1(8'h90), .D2(8'ha0), .D3(8'hb1), .D4(8'h17), .D5(8'h29), .D6(8'hd1),
    .D7(8'hdf), .Y(mux8to1x8_1_y));
  not not_1 (not_1_out, mux8to1x8_1_y[6]);
  and and_1 (and_1_out, mux8to1x8_1_y[6], mux8to1x8_1_y[7]);
  MUX2to1x2 mux2to1x2_1 (.S(and_1_out), .D0(mux8to1x8_1_y[3:2]), .D1(2'b00), .Y(mux2to1x2_1_y));
  // Probe on PC
  RegFile4x8 regfile4x8_1 (
    .clk(clock_1_out), .rs1(mux2to1x2_1_y), .rs2(mux8to1x8_1_y[1:0]), .rd(mux8to1x8_1_y[5:4]),
    .wen(not_1_out), .wdata(mux2to1x8_1_y), .rdata1(regfile4x8_1_rdata1), .rdata2(regfile4x8_1_rdata2));
  // Probe on mux2to1x8_1_y
  Adderx8 adderx8_1 (.A(regfile4x8_1_rdata1), .B(regfile4x8_1_rdata2), .cin(1'b0), .S(adderx8_1_s));  // open: C
  Cmpx8 cmpx8_1 (.A(regfile4x8_1_rdata1), .B(regfile4x8_1_rdata2), .eq(cmpx8_1_eq));
  not not_2 (not_2_out, cmpx8_1_eq);
  and and_2 (and_2_out, not_2_out, and_1_out);
  MUX2to1x8 mux2to1x8_1 (.S(mux8to1x8_1_y[7]), .D0(adderx8_1_s), .D1({4'b0000, mux8to1x8_1_y[3:0]}), .Y(mux2to1x8_1_y));
endmodule

module ImmGen (
  input  [31:0] inst,
  output [31:0] immI,
  output [31:0] immS,
  output [31:0] immU
);

  assign immI = {{20{inst[31]}}, inst[31:20]};  // Bit_Extender bit_extender_1
  assign immS = {{20{inst[31]}}, {inst[31:25], inst[11:7]}};  // Bit_Extender bit_extender_2

  assign immU = {inst[31:12], {12{1'b0}}};
endmodule

module RegFile32x32 (
  input  clk,
  input  [31:0] wdata,
  input  [4:0] waddr,
  input  wen,
  input  [4:0] raddr1,
  input  [4:0] raddr2,
  output [31:0] rdata1,
  output [31:0] rdata2
);

  wire decoder_1_out1, decoder_1_out2, decoder_1_out3, decoder_1_out4, decoder_1_out5, decoder_1_out6,
       decoder_1_out7, decoder_1_out8, decoder_1_out9, decoder_1_out10, decoder_1_out11, decoder_1_out12,
       decoder_1_out13, decoder_1_out14, decoder_1_out15, decoder_1_out16, decoder_1_out17, decoder_1_out18,
       decoder_1_out19, decoder_1_out20, decoder_1_out21, decoder_1_out22, decoder_1_out23, decoder_1_out24,
       decoder_1_out25, decoder_1_out26, decoder_1_out27, decoder_1_out28, decoder_1_out29, decoder_1_out30,
       decoder_1_out31;
  wire [31:0] r1_q, r2_q, r3_q, r8_q, r12_q, r16_q, r20_q, r24_q, r28_q, register_1_q, register_2_q,
       register_3_q, register_4_q, register_5_q, register_6_q, register_7_q, register_8_q, register_9_q,
       register_10_q, register_11_q, register_12_q, register_13_q, register_14_q, register_15_q,
       register_16_q, register_17_q, register_18_q, register_19_q, register_20_q, register_21_q,
       register_22_q;

  Decoder #(.select(5)) decoder_1 (
    .out1(decoder_1_out1), .out2(decoder_1_out2), .out3(decoder_1_out3), .out4(decoder_1_out4),
    .out5(decoder_1_out5), .out6(decoder_1_out6), .out7(decoder_1_out7), .out8(decoder_1_out8),
    .out9(decoder_1_out9), .out10(decoder_1_out10), .out11(decoder_1_out11), .out12(decoder_1_out12),
    .out13(decoder_1_out13), .out14(decoder_1_out14), .out15(decoder_1_out15), .out16(decoder_1_out16),
    .out17(decoder_1_out17), .out18(decoder_1_out18), .out19(decoder_1_out19), .out20(decoder_1_out20),
    .out21(decoder_1_out21), .out22(decoder_1_out22), .out23(decoder_1_out23), .out24(decoder_1_out24),
    .out25(decoder_1_out25), .out26(decoder_1_out26), .out27(decoder_1_out27), .out28(decoder_1_out28),
    .out29(decoder_1_out29), .out30(decoder_1_out30), .out31(decoder_1_out31), .sel(waddr), .en(wen));  // open: out0
  Register #(.width(32)) r16 (.D(wdata), .en(decoder_1_out16), .clk(clk), .Q(r16_q));  // open: clr
  Register #(.width(32)) r8 (.D(wdata), .en(decoder_1_out8), .clk(clk), .Q(r8_q));  // open: clr
  Register #(.width(32)) r24 (.D(wdata), .en(decoder_1_out24), .clk(clk), .Q(r24_q));  // open: clr
  Register #(.width(32)) r1 (.D(wdata), .en(decoder_1_out1), .clk(clk), .Q(r1_q));  // open: clr
  Register #(.width(32)) register_1 (.D(wdata), .en(decoder_1_out17), .clk(clk), .Q(register_1_q));  // open: clr
  Register #(.width(32)) register_2 (.D(wdata), .en(decoder_1_out9), .clk(clk), .Q(register_2_q));  // open: clr
  Register #(.width(32)) register_3 (.D(wdata), .en(decoder_1_out25), .clk(clk), .Q(register_3_q));  // open: clr
  Register #(.width(32)) r2 (.D(wdata), .en(decoder_1_out2), .clk(clk), .Q(r2_q));  // open: clr
  Register #(.width(32)) register_4 (.D(wdata), .en(decoder_1_out18), .clk(clk), .Q(register_4_q));  // open: clr
  Register #(.width(32)) register_5 (.D(wdata), .en(decoder_1_out10), .clk(clk), .Q(register_5_q));  // open: clr
  Register #(.width(32)) register_6 (.D(wdata), .en(decoder_1_out26), .clk(clk), .Q(register_6_q));  // open: clr
  Register #(.width(32)) r3 (.D(wdata), .en(decoder_1_out3), .clk(clk), .Q(r3_q));  // open: clr
  Register #(.width(32)) register_7 (.D(wdata), .en(decoder_1_out19), .clk(clk), .Q(register_7_q));  // open: clr
  Register #(.width(32)) register_8 (.D(wdata), .en(decoder_1_out11), .clk(clk), .Q(register_8_q));  // open: clr
  Register #(.width(32)) register_9 (.D(wdata), .en(decoder_1_out27), .clk(clk), .Q(register_9_q));  // open: clr
  Register #(.width(32)) register_10 (.D(wdata), .en(decoder_1_out4), .clk(clk), .Q(register_10_q));  // open: clr
  Register #(.width(32)) r20 (.D(wdata), .en(decoder_1_out20), .clk(clk), .Q(r20_q));  // open: clr
  Register #(.width(32)) r12 (.D(wdata), .en(decoder_1_out12), .clk(clk), .Q(r12_q));  // open: clr
  Register #(.width(32)) r28 (.D(wdata), .en(decoder_1_out28), .clk(clk), .Q(r28_q));  // open: clr
  Register #(.width(32)) register_11 (.D(wdata), .en(decoder_1_out5), .clk(clk), .Q(register_11_q));  // open: clr
  Register #(.width(32)) register_12 (.D(wdata), .en(decoder_1_out21), .clk(clk), .Q(register_12_q));  // open: clr
  Register #(.width(32)) register_13 (.D(wdata), .en(decoder_1_out13), .clk(clk), .Q(register_13_q));  // open: clr
  Register #(.width(32)) register_14 (.D(wdata), .en(decoder_1_out29), .clk(clk), .Q(register_14_q));  // open: clr
  Register #(.width(32)) register_15 (.D(wdata), .en(decoder_1_out6), .clk(clk), .Q(register_15_q));  // open: clr
  Register #(.width(32)) register_16 (.D(wdata), .en(decoder_1_out22), .clk(clk), .Q(register_16_q));  // open: clr
  Register #(.width(32)) register_17 (.D(wdata), .en(decoder_1_out14), .clk(clk), .Q(register_17_q));  // open: clr
  Register #(.width(32)) register_18 (.D(wdata), .en(decoder_1_out30), .clk(clk), .Q(register_18_q));  // open: clr
  Register #(.width(32)) register_19 (.D(wdata), .en(decoder_1_out7), .clk(clk), .Q(register_19_q));  // open: clr
  Register #(.width(32)) register_20 (.D(wdata), .en(decoder_1_out23), .clk(clk), .Q(register_20_q));  // open: clr
  Register #(.width(32)) register_21 (.D(wdata), .en(decoder_1_out15), .clk(clk), .Q(register_21_q));  // open: clr
  Register #(.width(32)) register_22 (.D(wdata), .en(decoder_1_out31), .clk(clk), .Q(register_22_q));  // open: clr
  Multiplexer #(.select(5), .width(32)) multiplexer_1 (
    .in0({32{1'b0}}), .in1(r1_q), .in2(r2_q), .in3(r3_q), .in4(register_10_q), .in5(register_11_q),
    .in6(register_15_q), .in7(register_19_q), .in8(r8_q), .in9(register_2_q), .in10(register_5_q),
    .in11(register_8_q), .in12(r12_q), .in13(register_13_q), .in14(register_17_q), .in15(register_21_q),
    .in16(r16_q), .in17(register_1_q), .in18(register_4_q), .in19(register_7_q), .in20(r20_q),
    .in21(register_12_q), .in22(register_16_q), .in23(register_20_q), .in24(r24_q), .in25(register_3_q),
    .in26(register_6_q), .in27(register_9_q), .in28(r28_q), .in29(register_14_q), .in30(register_18_q),
    .in31(register_22_q), .out(rdata1), .sel(raddr1));
  Multiplexer #(.select(5), .width(32)) multiplexer_2 (
    .in0({32{1'b0}}), .in1(r1_q), .in2(r2_q), .in3(r3_q), .in4(register_10_q), .in5(register_11_q),
    .in6(register_15_q), .in7(register_19_q), .in8(r8_q), .in9(register_2_q), .in10(register_5_q),
    .in11(register_8_q), .in12(r12_q), .in13(register_13_q), .in14(register_17_q), .in15(register_21_q),
    .in16(r16_q), .in17(register_1_q), .in18(register_4_q), .in19(register_7_q), .in20(r20_q),
    .in21(register_12_q), .in22(register_16_q), .in23(register_20_q), .in24(r24_q), .in25(register_3_q),
    .in26(register_6_q), .in27(register_9_q), .in28(r28_q), .in29(register_14_q), .in30(register_18_q),
    .in31(register_22_q), .out(rdata2), .sel(raddr2));
endmodule

module RegFile16x32 (
  input  clk,
  input  [31:0] wdata,
  input  [4:0] waddr,
  input  wen,
  input  [4:0] raddr1,
  input  [4:0] raddr2,
  output [31:0] rdata1,
  output [31:0] rdata2
);

  wire decoder_1_out1, decoder_1_out2, decoder_1_out3, decoder_1_out4, decoder_1_out5, decoder_1_out6,
       decoder_1_out7, decoder_1_out8, decoder_1_out9, decoder_1_out10, decoder_1_out11, decoder_1_out12,
       decoder_1_out13, decoder_1_out14, decoder_1_out15;
  wire [31:0] r1_q, r2_q, r3_q, r8_q, r12_q, register_1_q, register_2_q, register_3_q, register_4_q,
       register_5_q, register_6_q, register_7_q, register_8_q, register_9_q, register_10_q;

  Decoder #(.select(4)) decoder_1 (
    .out1(decoder_1_out1), .out2(decoder_1_out2), .out3(decoder_1_out3), .out4(decoder_1_out4),
    .out5(decoder_1_out5), .out6(decoder_1_out6), .out7(decoder_1_out7), .out8(decoder_1_out8),
    .out9(decoder_1_out9), .out10(decoder_1_out10), .out11(decoder_1_out11), .out12(decoder_1_out12),
    .out13(decoder_1_out13), .out14(decoder_1_out14), .out15(decoder_1_out15), .sel(waddr[3:0]), .en(wen));  // open: out0
  Register #(.width(32)) r8 (.D(wdata), .en(decoder_1_out8), .clk(clk), .Q(r8_q));  // open: clr
  Register #(.width(32)) r1 (.D(wdata), .en(decoder_1_out1), .clk(clk), .Q(r1_q));  // open: clr
  Register #(.width(32)) register_1 (.D(wdata), .en(decoder_1_out9), .clk(clk), .Q(register_1_q));  // open: clr
  Register #(.width(32)) r2 (.D(wdata), .en(decoder_1_out2), .clk(clk), .Q(r2_q));  // open: clr
  Register #(.width(32)) register_2 (.D(wdata), .en(decoder_1_out10), .clk(clk), .Q(register_2_q));  // open: clr
  Register #(.width(32)) r3 (.D(wdata), .en(decoder_1_out3), .clk(clk), .Q(r3_q));  // open: clr
  Register #(.width(32)) register_3 (.D(wdata), .en(decoder_1_out11), .clk(clk), .Q(register_3_q));  // open: clr
  Register #(.width(32)) register_4 (.D(wdata), .en(decoder_1_out4), .clk(clk), .Q(register_4_q));  // open: clr
  Register #(.width(32)) r12 (.D(wdata), .en(decoder_1_out12), .clk(clk), .Q(r12_q));  // open: clr
  Register #(.width(32)) register_5 (.D(wdata), .en(decoder_1_out5), .clk(clk), .Q(register_5_q));  // open: clr
  Register #(.width(32)) register_6 (.D(wdata), .en(decoder_1_out13), .clk(clk), .Q(register_6_q));  // open: clr
  Register #(.width(32)) register_7 (.D(wdata), .en(decoder_1_out6), .clk(clk), .Q(register_7_q));  // open: clr
  Register #(.width(32)) register_8 (.D(wdata), .en(decoder_1_out14), .clk(clk), .Q(register_8_q));  // open: clr
  Register #(.width(32)) register_9 (.D(wdata), .en(decoder_1_out7), .clk(clk), .Q(register_9_q));  // open: clr
  Register #(.width(32)) register_10 (.D(wdata), .en(decoder_1_out15), .clk(clk), .Q(register_10_q));  // open: clr
  Multiplexer #(.select(4), .width(32)) multiplexer_1 (
    .in0({32{1'b0}}), .in1(r1_q), .in2(r2_q), .in3(r3_q), .in4(register_4_q), .in5(register_5_q),
    .in6(register_7_q), .in7(register_9_q), .in8(r8_q), .in9(register_1_q), .in10(register_2_q),
    .in11(register_3_q), .in12(r12_q), .in13(register_6_q), .in14(register_8_q), .in15(register_10_q),
    .out(rdata1), .sel(raddr1[3:0]));
  Multiplexer #(.select(4), .width(32)) multiplexer_2 (
    .in0({32{1'b0}}), .in1(r1_q), .in2(r2_q), .in3(r3_q), .in4(register_4_q), .in5(register_5_q),
    .in6(register_7_q), .in7(register_9_q), .in8(r8_q), .in9(register_1_q), .in10(register_2_q),
    .in11(register_3_q), .in12(r12_q), .in13(register_6_q), .in14(register_8_q), .in15(register_10_q),
    .out(rdata2), .sel(raddr2[3:0]));
endmodule

module InstDecode (
  input  [31:0] inst,
  output isJalr,
  output isStype,
  output isRtype,
  output isLui,
  output isLoad
);

  wire comparator_1_eq, comparator_2_eq, comparator_4_eq, comparator_5_eq;

  Comparator #(.width(7)) comparator_1 (.a(inst[6:0]), .b(7'b1100111), .eq(comparator_1_eq));  // open: gt, lt
  Comparator #(.width(3)) comparator_2 (.a(inst[14:12]), .b(3'b000), .eq(comparator_2_eq));  // open: gt, lt
  Comparator #(.width(7)) comparator_3 (.a(inst[6:0]), .b(7'b0100011), .eq(isStype));  // open: gt, lt
  Comparator #(.width(7)) comparator_4 (.a(inst[6:0]), .b(7'b0110011), .eq(comparator_4_eq));  // open: gt, lt
  Comparator #(.width(7)) comparator_5 (.a(inst[31:25]), .b({7{1'b0}}), .eq(comparator_5_eq));  // open: gt, lt
  Comparator #(.width(7)) comparator_6 (.a(inst[6:0]), .b(7'b0110111), .eq(isLui));  // open: gt, lt
  Comparator #(.width(7)) comparator_7 (.a(inst[6:0]), .b(7'b0000011), .eq(isLoad));  // open: gt, lt
  and and_1 (isJalr, comparator_1_eq, comparator_2_eq);
  and and_2 (isRtype, comparator_4_eq, comparator_2_eq, comparator_5_eq);
endmodule

module addressDecoder (
  input  [31:0] addr,
  output isVGA,
  output isMem
);

  Comparator #(.width(14)) comparator_1 (.a(addr[31:18]), .b(14'h800), .eq(isVGA));  // open: gt, lt
  not not_1 (isMem, isVGA);
endmodule

module rv32mini (
);

  wire addressdecoder_1_ismem, addressdecoder_1_isvga, and_2_out, clock_1_out, comparator_1_eq,
       comparator_2_eq, dipswitch_1_sw3, instdecode_1_isjalr, instdecode_1_isload, instdecode_1_islui,
       instdecode_1_isrtype, instdecode_1_isstype, not_1_out, wenVGA;
  wire [1:0] adder_3_out;
  wire [3:0] decoder_1_out0, multiplexer_5_out;
  wire [7:0] multiplexer_8_out, regfile16x32_1_rdata2_2;
  wire [9:0] adder_3_out_3;
  wire [19:0] adder_3_out_2;
  wire [23:0] regfile16x32_1_rdata2;
  wire [31:0] adder_1_out, bit_extender_1_out, immgen_1_immi, immgen_1_imms, immgen_1_immu,
       multiplexer_1_out, multiplexer_2_out, multiplexer_3_out, multiplexer_4_out, multiplexer_6_out,
       multiplexer_7_out, multiplexer_9_out, multiplexer_10_out, PC_q, ram_1_dout, regfile16x32_1_rdata1,
       rom_1_data;
  wire [63:0] adder_2_out, register_1_q;

  Clock clock_1 (.out(clock_1_out));
  Register #(.width(32)) PC (.D(multiplexer_1_out), .en(1'b1), .clk(clock_1_out), .Q(PC_q), .clr(dipswitch_1_sw3));
  DipSwitch dipswitch_1 (.sw3(dipswitch_1_sw3));  // open: sw1, sw2, sw4, sw5, sw6, sw7, sw8
  Adder #(.width(32)) adder_1 (.a(32'h4), .b(PC_q), .out(adder_1_out), .cin(1'b0));  // open: cout
  ROM #(.addrWidth(20), .dataWidth(32)) rom_1 (.addr(PC_q[21:2]), .data(rom_1_data));
  Register #(.width(64)) register_1 (
    .D(adder_2_out), .en(1'b1), .clk(clock_1_out), .Q(register_1_q), .clr(dipswitch_1_sw3));
  Multiplexer #(.width(32)) multiplexer_1 (
    .in0(adder_1_out), .in1({adder_3_out_3, adder_3_out_2, adder_3_out}), .out(multiplexer_1_out),
    .sel(instdecode_1_isjalr));
  // Probe on register_1_q
  Adder #(.width(64)) adder_2 (.a(64'h1), .b(register_1_q), .out(adder_2_out), .cin(1'b0));  // open: cout
  not not_1 (not_1_out, instdecode_1_isstype);
  InstDecode instdecode_1 (
    .inst(rom_1_data), .isJalr(instdecode_1_isjalr), .isStype(instdecode_1_isstype),
    .isRtype(instdecode_1_isrtype), .isLui(instdecode_1_islui), .isLoad(instdecode_1_isload));
  ImmGen immgen_1 (.inst(rom_1_data), .immI(immgen_1_immi), .immS(immgen_1_imms), .immU(immgen_1_immu));
  Multiplexer #(.width(32)) multiplexer_2 (
    .in0(immgen_1_immi), .in1(immgen_1_imms), .out(multiplexer_2_out), .sel(instdecode_1_isstype));
  RegFile16x32 regfile16x32_1 (
    .clk(clock_1_out), .wdata(multiplexer_10_out), .waddr(rom_1_data[11:7]), .wen(not_1_out),
    .raddr1(rom_1_data[19:15]), .raddr2(rom_1_data[24:20]), .rdata1(regfile16x32_1_rdata1),
    .rdata2({regfile16x32_1_rdata2_2, regfile16x32_1_rdata2}));
  Decoder #(.enable("false"), .select(2)) decoder_1 (
    .out0(decoder_1_out0[0]), .out1(decoder_1_out0[1]), .out2(decoder_1_out0[2]), .out3(decoder_1_out0[3]),
    .sel(adder_3_out));
  Multiplexer #(.width(32)) multiplexer_3 (
    .in0(multiplexer_2_out), .in1({regfile16x32_1_rdata2_2, regfile16x32_1_rdata2}), .out(multiplexer_3_out),
    .sel(instdecode_1_isrtype));
  Comparator #(.width(3)) comparator_1 (.a(3'b000), .b(rom_1_data[14:12]), .eq(comparator_1_eq));  // open: gt, lt
  Multiplexer #(.width(32)) multiplexer_4 (
    .in0({regfile16x32_1_rdata2_2, regfile16x32_1_rdata2}),
    .in1({regfile16x32_1_rdata2[7:0], regfile16x32_1_rdata2[7:0], regfile16x32_1_rdata2[7:0], regfile16x32_1_rdata2[7:0]}),
    .out(multiplexer_4_out), .sel(comparator_1_eq));
  Adder #(.width(32)) adder_3 (
    .a(regfile16x32_1_rdata1), .b(multiplexer_3_out), .out({adder_3_out_3, adder_3_out_2, adder_3_out}),
    .cin(1'b0));  // open: cout
  Multiplexer #(.width(4)) multiplexer_5 (
    .in0(4'b1111), .in1(decoder_1_out0), .out(multiplexer_5_out), .sel(comparator_1_eq));
  Multiplexer #(.width(32)) multiplexer_6 (
    .in0({adder_3_out_3, adder_3_out_2, adder_3_out}), .in1(adder_1_out), .out(multiplexer_6_out),
    .sel(instdecode_1_isjalr));
  RAM #(.addrWidth(20), .asyncread("true"), .byteenables("byteEnables"), .dataWidth(32), .\type ("nonvolatile")) ram_1 (
    .addr(adder_3_out_2), .we(and_2_out), .oe(1'b1), .clk(clock_1_out), .din(multiplexer_4_out),
    .dout(ram_1_dout), .be3(multiplexer_5_out[3]), .be2(multiplexer_5_out[2]), .be1(multiplexer_5_out[1]),
    .be0(multiplexer_5_out[0]));
  Multiplexer #(.width(32)) multiplexer_7 (
    .in0(multiplexer_6_out), .in1(immgen_1_immu), .out(multiplexer_7_out), .sel(instdecode_1_islui));
  Comparator #(.width(3)) comparator_2 (.a(rom_1_data[14:12]), .b(3'b100), .eq(comparator_2_eq));  // open: gt, lt
  addressDecoder addressdecoder_1 (
    .addr({adder_3_out_3, adder_3_out_2, adder_3_out}), .isVGA(addressdecoder_1_isvga),
    .isMem(addressdecoder_1_ismem));
  Multiplexer #(.select(2), .width(8)) multiplexer_8 (
    .in0(ram_1_dout[7:0]), .in1(ram_1_dout[15:8]), .in2(ram_1_dout[23:16]), .in3(ram_1_dout[31:24]),
    .out(multiplexer_8_out), .sel(adder_3_out));
  and and_1 (wenVGA, addressdecoder_1_isvga, instdecode_1_isstype);
  and and_2 (and_2_out, addressdecoder_1_ismem, instdecode_1_isstype);
  assign bit_extender_1_out = {{24{1'b0}}, multiplexer_8_out};  // Bit_Extender bit_extender_1
  Multiplexer #(.width(32)) multiplexer_9 (
    .in0(ram_1_dout), .in1(bit_extender_1_out), .out(multiplexer_9_out), .sel(comparator_2_eq));
  Multiplexer #(.width(32)) multiplexer_10 (
    .in0(multiplexer_7_out), .in1(multiplexer_9_out), .out(multiplexer_10_out), .sel(instdecode_1_isload));
  // RGB_Video #(.cursor("No Cursor"), .height(256), .scale(1), .width(256)) rgb_video_1: pin names not known; wires that end beside it: dipswitch_1_sw3, clock_1_out, wenVGA, adder_3_out_2[7:0], adder_3_out_2[15:8], regfile16x32_1_rdata2

  // Notes on the sheet:
  //   contents of rom_1 (hex, n*v repeats v):
  //   413 93137 10113 10b7 dbc08093 80e7 fe012823 fea10923 fea12423 fe914203 fe4109a3 ff012783 f787b3
  //   f787b3 4b6b7 af868693 fdc10113 d787b3 10000713 f12423 10593 100793 b00513 2112023 12023 12223 e12623
  //   e12823 f10a23 10b7 a8408093 80e7 2012083 2410113 8067 ff410113 112423 10b7 a7c08093 80e7 513 1800093
  //   80e7 812083 513 c10113 8067 852583 feb12823 fe812e23 3437 80840413 ff014183 3401b3 1c183 ff114203
  //   440233 24203 4181b3 ff214203 440233 24203 4181b3 ff314203 440233 24203 4181b3 3237 80020213 320233
  //   24203 ffc12403 420233 420233 410233 11b7 86418193 fe312823 14800193 fe312623 fec22203 20067 1052703
  //   52683 452783 fe810113 e12423 112a23 812823 912623 fed12823 fef12623 13737 a0070713 fe012223 ff314203
  //   fe4102a3 fef14203 fe410223 fe412203 470233 24203 fe4105a3 ff214203 fe4102a3 fee14203 fe410223
  //   fe412203 470233 24203 fe410523 ff114203 fe4102a3 fed14203 fe410223 fe412203 470233 24203 fe4104a3
  //   ff014203 fe4102a3 fec14203 fe410223 fe412203 470233 24203 fe410423 fe812703 c52603 fee12823 fe812e23
  //   3437 80840413 ff014183 3401b3 1c183 ff114203 440233 24203 4181b3 ff214203 440233 24203 4181b3
  //   ff314203 440233 24203 4181b3 3237 80020213 320233 24203 ffc12403 420233 420233 410233 66800193
  //   fe312823 28800193 fe312623 fec22203 20067 c68733 10000513 fe812e23 fe912c23 fee12823 50413 ff012483
  //   fe812423 feb14183 3181b3 fe312423 fe914183 3181b3 fe912423 feb14203 420233 fe412423 fe914203 4181b3
  //   3181b3 fe312a23 fe912423 33237 90020213 feb14183 4181b3 1c183 fe3103a3 fea14183 4181b3 1c183
  //   fe310323 fe914183 4181b3 1c183 fe3102a3 fe814183 4181b3 1c183 fe310223 ff412183 fe412203 440233
  //   120213 fe412423 feb14203 420233 fe412423 fe914203 4181b3 3237 90820213 320233 ff812483 ffc12403
  //   24203 420233 420233 410233 11b7 86818193 fe312823 39000193 fe312623 fec22203 20067 812703 10000513
  //   e78733 fe812e23 fe912c23 fee12823 50413 ff012483 fe812423 feb14183 3181b3 fe312423 fe914183 3181b3
  //   fe912423 feb14203 420233 fe412423 fe914203 4181b3 3181b3 fe312a23 fe912423 33237 90020213 feb14183
  //   4181b3 1c183 fe3103a3 fea14183 4181b3 1c183 fe310323 fe914183 4181b3 1c183 fe3102a3 fe814183 4181b3
  //   1c183 fe310223 ff412183 fe412203 440233 120213 fe412423 feb14203 420233 fe412423 fe914203 4181b3
  //   3237 90820213 320233 ff812483 ffc12403 24203 420233 420233 410233 11b7 86818193 fe312823 49c00193
  //   fe312623 fec22203 20067 8*f787b3 d787b3 f787b3 f787b3 20000437 f40433 812783 c60633 c60633 fef12423
  //   feb14183 3181b3 fe312423 fe914183 fff78213 fe412423 feb14203 420233 fe412423 fe914203 4181b3 3237
  //   91820213 418233 24203 420233 420233 410233 65400193 fe312823 54000193 fe312623 fec22203 20067 493
  //   40513 b12223 c12023 10b7 de008093 80e7 12603 412583 812783 148493 40040413 c585b3 fef12823 fe912623
  //   fe812e23 fe912c23 2437 70040413 ff014183 340233 100193 320023 fec14183 3401b3 18023 24183 ff114483
  //   940233 100493 920023 fed14483 9404b3 48023 24483 9181b3 ff214483 940233 100493 920023 fee14483
  //   9404b3 48023 24483 9181b3 ff314483 940233 100493 920023 fef14483 9404b3 48023 24483 9181b3 3237
  //   80020213 320233 24203 ff812483 ffc12403 420233 420233 410233 65400193 fe312823 54400193 fe312623
  //   fec22203 20067 1412083 1012403 c12483 1810113 8067 10000713 fec12823 fee12623 fe812e23 fe912c23 2437
  //   70040413 ff014183 340233 100193 320023 fec14183 3401b3 18023 24183 ff114483 940233 100493 920023
  //   fed14483 9404b3 48023 24483 9181b3 ff214483 940233 100493 920023 fee14483 9404b3 48023 24483 9181b3
  //   ff314483 940233 100493 920023 fef14483 9404b3 48023 24483 9181b3 3237 80020213 320233 24203 ff812483
  //   ffc12403 420233 420233 410233 74c00193 fe312823 28800193 fe312623 fec22203 20067 812703 fee12823
  //   fec12623 fe812e23 fe912c23 2437 70040413 ff014183 340233 100193 320023 fec14183 3401b3 18023 24183
  //   ff114483 940233 100493 920023 fed14483 9404b3 48023 24483 9181b3 ff214483 940233 100493 920023
  //   fee14483 9404b3 48023 24483 9181b3 ff314483 940233 100493 920023 fef14483 9404b3 48023 24483 9181b3
  //   3237 80020213 320233 24203 ff812483 ffc12403 420233 420233 410233 11b7 83418193 fe312823 39000193
  //   fe312623 fec22203 20067 1012403 1412083 c12483 40637 20000537 1810113 1237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
endmodule
