// Logisim project test.circ as structural Verilog: 10 circuits, main circuit main
module main (
  input  rst,
  output [3:0] out_2
);

  wire clock_1_out;
  wire [3:0] adderx4_1_s;

  Clock clock_1 (.out(clock_1_out));
  Regx4 regx4_1 (.D(adderx4_1_s), .rst(rst), .clk(clock_1_out), .out_4(out_2));
  Adderx4 adderx4_1 (.A(out_2), .B(4'b0001), .Cin(1'b0), .S(adderx4_1_s));  // open: Cout
endmodule

module MUX2to1 (
  input  A,
  input  B,
  input  S,
  output cout
);

  wire and_1_out, and_2_out, not_1_out;

  not not_1 (not_1_out, S);
  and and_1 (and_1_out, A, not_1_out);
  and and_2 (and_2_out, B, S);
  or or_1 (cout, and_1_out, and_2_out);
endmodule

module SR_Latch (
  input  S,
  input  R,
  output Q,
  output NQ
);

  nor nor_1 (Q, R, NQ);
  nor nor_2 (NQ, Q, S);
endmodule

module D_Latch (
  input  D,
  input  Enable,
  output Q,
  output NQ
);

  wire and_1_out, and_2_out, not_1_out;

  not not_1 (not_1_out, D);
  and and_1 (and_1_out, Enable, D);
  and and_2 (and_2_out, Enable, not_1_out);
  SR_Latch sr_latch_1 (.S(and_1_out), .R(and_2_out), .Q(Q), .NQ(NQ));
endmodule

module DFF (
  input  D,
  input  clk,
  output out_3
);

  wire d_latch_1_q, not_1_out;

  not not_1 (not_1_out, clk);
  D_Latch d_latch_1 (.D(D), .Enable(clk), .Q(d_latch_1_q));  // open: NQ
  D_Latch d_latch_2 (.D(d_latch_1_q), .Enable(not_1_out), .Q(out_3));  // open: NQ
endmodule

module DFFR (
  input  D,
  input  rst,
  input  clk,
  output out_4
);

  wire mux2to1_1_cout;

  MUX2to1 mux2to1_1 (.A(D), .B(1'b0), .S(rst), .cout(mux2to1_1_cout));
  DFF dff_1 (.D(mux2to1_1_cout), .clk(clk), .out_3(out_4));
endmodule

module Regx4 (
  input  [3:0] D,
  input  rst,
  input  clk,
  output [3:0] out_4
);

  DFFR dffr_1 (.D(D[0]), .rst(rst), .clk(clk), .out_4(out_4[0]));
  DFFR dffr_2 (.D(D[1]), .rst(rst), .clk(clk), .out_4(out_4[1]));
  DFFR dffr_3 (.D(D[2]), .rst(rst), .clk(clk), .out_4(out_4[2]));
  DFFR dffr_4 (.D(D[3]), .rst(rst), .clk(clk), .out_4(out_4[3]));
endmodule

module HA (
  input  A,
  input  B,
  output S,
  output C
);

  xor xor_1 (S, A, B);
  and and_1 (C, A, B);
endmodule

module FA (
  input  A,
  input  B,
  input  Cin,
  output S,
  output Cout
);

  wire ha_1_c, ha_1_s, ha_2_c;

  HA ha_1 (.A(A), .B(B), .S(ha_1_s), .C(ha_1_c));
  HA ha_2 (.A(ha_1_s), .B(Cin), .S(S), .C(ha_2_c));
  or or_1 (Cout, ha_1_c, ha_2_c);
endmodule

module Adderx4 (
  input  [3:0] A,
  input  [3:0] B,
  input  Cin,
  output [3:0] S,
  output Cout
);

  wire fa_1_cout, fa_2_cout, fa_3_cout;

  FA fa_1 (.A(A[0]), .B(B[0]), .Cin(Cin), .S(S[0]), .Cout(fa_1_cout));
  FA fa_2 (.A(A[1]), .B(B[1]), .Cin(fa_1_cout), .S(S[1]), .Cout(fa_2_cout));
  FA fa_3 (.A(A[2]), .B(B[2]), .Cin(fa_2_cout), .S(S[2]), .Cout(fa_3_cout));
  FA fa_4 (.A(A[3]), .B(B[3]), .Cin(fa_3_cout), .S(S[3]), .Cout(Cout));
endmodule
